// Logisim project 32B ALU.circ as structural Verilog: 18 circuits, main circuit main
module Full_Adder (
  input  Carry_In,
  input  A,
  input  B,
  output Result,
  output Carry_out
);

  wire and_1_out, and_2_out, xor_1_out;

  xor xor_1 (xor_1_out, A, B);
  and and_1 (and_1_out, B, A);
  and and_2 (and_2_out, xor_1_out, Carry_In);
  xor xor_2 (Result, Carry_In, xor_1_out);
  or or_1 (Carry_out, and_2_out, and_1_out);
endmodule

module OR_32 (
  input  [31:0] _32B_A,
  input  [31:0] _32b_B,
  output [31:0] A___B_32B
);

  or or_1 (A___B_32B[0], _32B_A[0], _32b_B[0]);
  or or_2 (A___B_32B[1], _32B_A[1], _32b_B[1]);
  or or_3 (A___B_32B[2], _32B_A[2], _32b_B[2]);
  or or_4 (A___B_32B[3], _32B_A[3], _32b_B[3]);
  or or_5 (A___B_32B[4], _32B_A[4], _32b_B[4]);
  or or_6 (A___B_32B[5], _32B_A[5], _32b_B[5]);
  or or_7 (A___B_32B[6], _32B_A[6], _32b_B[6]);
  or or_8 (A___B_32B[7], _32B_A[7], _32b_B[7]);
  or or_9 (A___B_32B[8], _32B_A[8], _32b_B[8]);
  or or_10 (A___B_32B[9], _32B_A[9], _32b_B[9]);
  or or_11 (A___B_32B[10], _32B_A[10], _32b_B[10]);
  or or_12 (A___B_32B[11], _32B_A[11], _32b_B[11]);
  or or_13 (A___B_32B[12], _32B_A[12], _32b_B[12]);
  or or_14 (A___B_32B[13], _32B_A[13], _32b_B[13]);
  or or_15 (A___B_32B[14], _32B_A[14], _32b_B[14]);
  or or_16 (A___B_32B[15], _32B_A[15], _32b_B[15]);
  or or_17 (A___B_32B[16], _32B_A[16], _32b_B[16]);
  or or_18 (A___B_32B[17], _32B_A[17], _32b_B[17]);
  or or_19 (A___B_32B[18], _32B_A[18], _32b_B[18]);
  or or_20 (A___B_32B[19], _32B_A[19], _32b_B[19]);
  or or_21 (A___B_32B[20], _32B_A[20], _32b_B[20]);
  or or_22 (A___B_32B[21], _32B_A[21], _32b_B[21]);
  or or_23 (A___B_32B[22], _32B_A[22], _32b_B[22]);
  or or_24 (A___B_32B[23], _32B_A[23], _32b_B[23]);
  or or_25 (A___B_32B[24], _32B_A[24], _32b_B[24]);
  or or_26 (A___B_32B[25], _32B_A[25], _32b_B[25]);
  or or_27 (A___B_32B[26], _32B_A[26], _32b_B[26]);
  or or_28 (A___B_32B[27], _32B_A[27], _32b_B[27]);
  or or_29 (A___B_32B[28], _32B_A[28], _32b_B[28]);
  or or_30 (A___B_32B[29], _32B_A[29], _32b_B[29]);
  or or_31 (A___B_32B[30], _32B_A[30], _32b_B[30]);
  or or_32 (A___B_32B[31], _32B_A[31], _32b_B[31]);
endmodule

module NOT_32 (
  input  [31:0] _32B_in,
  output [31:0] NOT_32B
);

  not not_1 (NOT_32B[0], _32B_in[0]);
  not not_2 (NOT_32B[1], _32B_in[1]);
  not not_3 (NOT_32B[2], _32B_in[2]);
  not not_4 (NOT_32B[3], _32B_in[3]);
  not not_5 (NOT_32B[4], _32B_in[4]);
  not not_6 (NOT_32B[5], _32B_in[5]);
  not not_7 (NOT_32B[6], _32B_in[6]);
  not not_8 (NOT_32B[7], _32B_in[7]);
  not not_9 (NOT_32B[8], _32B_in[8]);
  not not_10 (NOT_32B[9], _32B_in[9]);
  not not_11 (NOT_32B[10], _32B_in[10]);
  not not_12 (NOT_32B[11], _32B_in[11]);
  not not_13 (NOT_32B[12], _32B_in[12]);
  not not_14 (NOT_32B[13], _32B_in[13]);
  not not_15 (NOT_32B[14], _32B_in[14]);
  not not_16 (NOT_32B[15], _32B_in[15]);
  not not_17 (NOT_32B[16], _32B_in[16]);
  not not_18 (NOT_32B[17], _32B_in[17]);
  not not_19 (NOT_32B[18], _32B_in[18]);
  not not_20 (NOT_32B[19], _32B_in[19]);
  not not_21 (NOT_32B[20], _32B_in[20]);
  not not_22 (NOT_32B[21], _32B_in[21]);
  not not_23 (NOT_32B[22], _32B_in[22]);
  not not_24 (NOT_32B[23], _32B_in[23]);
  not not_25 (NOT_32B[24], _32B_in[24]);
  not not_26 (NOT_32B[25], _32B_in[25]);
  not not_27 (NOT_32B[26], _32B_in[26]);
  not not_28 (NOT_32B[27], _32B_in[27]);
  not not_29 (NOT_32B[28], _32B_in[28]);
  not not_30 (NOT_32B[29], _32B_in[29]);
  not not_31 (NOT_32B[30], _32B_in[30]);
  not not_32 (NOT_32B[31], _32B_in[31]);
endmodule

module XOR_32 (
  input  [31:0] _32B_A,
  input  [31:0] _32b_B,
  output [31:0] A___B_32B
);

  xor xor_1 (A___B_32B[0], _32B_A[0], _32b_B[0]);
  xor xor_2 (A___B_32B[1], _32B_A[1], _32b_B[1]);
  xor xor_3 (A___B_32B[2], _32B_A[2], _32b_B[2]);
  xor xor_4 (A___B_32B[3], _32B_A[3], _32b_B[3]);
  xor xor_5 (A___B_32B[4], _32B_A[4], _32b_B[4]);
  xor xor_6 (A___B_32B[5], _32B_A[5], _32b_B[5]);
  xor xor_7 (A___B_32B[6], _32B_A[6], _32b_B[6]);
  xor xor_8 (A___B_32B[7], _32B_A[7], _32b_B[7]);
  xor xor_9 (A___B_32B[8], _32B_A[8], _32b_B[8]);
  xor xor_10 (A___B_32B[9], _32B_A[9], _32b_B[9]);
  xor xor_11 (A___B_32B[10], _32B_A[10], _32b_B[10]);
  xor xor_12 (A___B_32B[11], _32B_A[11], _32b_B[11]);
  xor xor_13 (A___B_32B[12], _32B_A[12], _32b_B[12]);
  xor xor_14 (A___B_32B[13], _32B_A[13], _32b_B[13]);
  xor xor_15 (A___B_32B[14], _32B_A[14], _32b_B[14]);
  xor xor_16 (A___B_32B[15], _32B_A[15], _32b_B[15]);
  xor xor_17 (A___B_32B[16], _32B_A[16], _32b_B[16]);
  xor xor_18 (A___B_32B[17], _32B_A[17], _32b_B[17]);
  xor xor_19 (A___B_32B[18], _32B_A[18], _32b_B[18]);
  xor xor_20 (A___B_32B[19], _32B_A[19], _32b_B[19]);
  xor xor_21 (A___B_32B[20], _32B_A[20], _32b_B[20]);
  xor xor_22 (A___B_32B[21], _32B_A[21], _32b_B[21]);
  xor xor_23 (A___B_32B[22], _32B_A[22], _32b_B[22]);
  xor xor_24 (A___B_32B[23], _32B_A[23], _32b_B[23]);
  xor xor_25 (A___B_32B[24], _32B_A[24], _32b_B[24]);
  xor xor_26 (A___B_32B[25], _32B_A[25], _32b_B[25]);
  xor xor_27 (A___B_32B[26], _32B_A[26], _32b_B[26]);
  xor xor_28 (A___B_32B[27], _32B_A[27], _32b_B[27]);
  xor xor_29 (A___B_32B[28], _32B_A[28], _32b_B[28]);
  xor xor_30 (A___B_32B[29], _32B_A[29], _32b_B[29]);
  xor xor_31 (A___B_32B[30], _32B_A[30], _32b_B[30]);
  xor xor_32 (A___B_32B[31], _32B_A[31], _32b_B[31]);
endmodule

module AND_32 (
  input  [31:0] _32B_A,
  input  [31:0] _32b_B,
  output [31:0] A___B_32B
);

  and _0 (A___B_32B[0], _32B_A[0], _32b_B[0]);
  and _1 (A___B_32B[1], _32B_A[1], _32b_B[1]);
  and _2 (A___B_32B[2], _32B_A[2], _32b_B[2]);
  and _3 (A___B_32B[3], _32B_A[3], _32b_B[3]);
  and _4 (A___B_32B[4], _32B_A[4], _32b_B[4]);
  and _5 (A___B_32B[5], _32B_A[5], _32b_B[5]);
  and _6 (A___B_32B[6], _32B_A[6], _32b_B[6]);
  and _7 (A___B_32B[7], _32B_A[7], _32b_B[7]);
  and _8 (A___B_32B[8], _32B_A[8], _32b_B[8]);
  and _9 (A___B_32B[9], _32B_A[9], _32b_B[9]);
  and _10 (A___B_32B[10], _32B_A[10], _32b_B[10]);
  and _11 (A___B_32B[11], _32B_A[11], _32b_B[11]);
  and _12 (A___B_32B[12], _32B_A[12], _32b_B[12]);
  and _13 (A___B_32B[13], _32B_A[13], _32b_B[13]);
  and _14 (A___B_32B[14], _32B_A[14], _32b_B[14]);
  and _15 (A___B_32B[15], _32B_A[15], _32b_B[15]);
  and _16 (A___B_32B[16], _32B_A[16], _32b_B[16]);
  and _17 (A___B_32B[17], _32B_A[17], _32b_B[17]);
  and _18 (A___B_32B[18], _32B_A[18], _32b_B[18]);
  and _19 (A___B_32B[19], _32B_A[19], _32b_B[19]);
  and _20 (A___B_32B[20], _32B_A[20], _32b_B[20]);
  and _21 (A___B_32B[21], _32B_A[21], _32b_B[21]);
  and _22 (A___B_32B[22], _32B_A[22], _32b_B[22]);
  and _23 (A___B_32B[23], _32B_A[23], _32b_B[23]);
  and _24 (A___B_32B[24], _32B_A[24], _32b_B[24]);
  and _25 (A___B_32B[25], _32B_A[25], _32b_B[25]);
  and _26 (A___B_32B[26], _32B_A[26], _32b_B[26]);
  and _27 (A___B_32B[27], _32B_A[27], _32b_B[27]);
  and _28 (A___B_32B[28], _32B_A[28], _32b_B[28]);
  and _29 (A___B_32B[29], _32B_A[29], _32b_B[29]);
  and _30 (A___B_32B[30], _32B_A[30], _32b_B[30]);
  and _31 (A___B_32B[31], _32B_A[31], _32b_B[31]);
endmodule

module NOR_32 (
  input  [31:0] _32B_A,
  input  [31:0] _32b_B,
  output [31:0] A___B_32B
);

  nor nor_1 (A___B_32B[0], _32B_A[0], _32b_B[0]);
  nor nor_2 (A___B_32B[1], _32B_A[1], _32b_B[1]);
  nor nor_3 (A___B_32B[2], _32B_A[2], _32b_B[2]);
  nor nor_4 (A___B_32B[3], _32B_A[3], _32b_B[3]);
  nor nor_5 (A___B_32B[4], _32B_A[4], _32b_B[4]);
  nor nor_6 (A___B_32B[5], _32B_A[5], _32b_B[5]);
  nor nor_7 (A___B_32B[6], _32B_A[6], _32b_B[6]);
  nor nor_8 (A___B_32B[7], _32B_A[7], _32b_B[7]);
  nor nor_9 (A___B_32B[8], _32B_A[8], _32b_B[8]);
  nor nor_10 (A___B_32B[9], _32B_A[9], _32b_B[9]);
  nor nor_11 (A___B_32B[10], _32B_A[10], _32b_B[10]);
  nor nor_12 (A___B_32B[11], _32B_A[11], _32b_B[11]);
  nor nor_13 (A___B_32B[12], _32B_A[12], _32b_B[12]);
  nor nor_14 (A___B_32B[13], _32B_A[13], _32b_B[13]);
  nor nor_15 (A___B_32B[14], _32B_A[14], _32b_B[14]);
  nor nor_16 (A___B_32B[15], _32B_A[15], _32b_B[15]);
  nor nor_17 (A___B_32B[16], _32B_A[16], _32b_B[16]);
  nor nor_18 (A___B_32B[17], _32B_A[17], _32b_B[17]);
  nor nor_19 (A___B_32B[18], _32B_A[18], _32b_B[18]);
  nor nor_20 (A___B_32B[19], _32B_A[19], _32b_B[19]);
  nor nor_21 (A___B_32B[20], _32B_A[20], _32b_B[20]);
  nor nor_22 (A___B_32B[21], _32B_A[21], _32b_B[21]);
  nor nor_23 (A___B_32B[22], _32B_A[22], _32b_B[22]);
  nor nor_24 (A___B_32B[23], _32B_A[23], _32b_B[23]);
  nor nor_25 (A___B_32B[24], _32B_A[24], _32b_B[24]);
  nor nor_26 (A___B_32B[25], _32B_A[25], _32b_B[25]);
  nor nor_27 (A___B_32B[26], _32B_A[26], _32b_B[26]);
  nor nor_28 (A___B_32B[27], _32B_A[27], _32b_B[27]);
  nor nor_29 (A___B_32B[28], _32B_A[28], _32b_B[28]);
  nor nor_30 (A___B_32B[29], _32B_A[29], _32b_B[29]);
  nor nor_31 (A___B_32B[30], _32B_A[30], _32b_B[30]);
  nor nor_32 (A___B_32B[31], _32B_A[31], _32b_B[31]);
endmodule

module Logical32 (
  input  [31:0] in_1,
  input  [31:0] in_2,
  input  [1:0] in_3,
  output [31:0] out_4
);

  wire [31:0] and_1_out, nor_1_out, or_1_out, xor_1_out;

  assign and_1_out = in_1 & in_2;  // AND_Gate and_1, 32 bits wide
  assign or_1_out = in_1 | in_2;  // OR_Gate or_1, 32 bits wide
  Multiplexer #(.select(2), .width(32)) multiplexer_1 (
    .in0(and_1_out), .in1(or_1_out), .in2(nor_1_out), .in3(xor_1_out), .out(out_4), .sel(in_3));  // open: en
  assign nor_1_out = ~(in_1 | in_2);  // NOR_Gate nor_1, 32 bits wide
  assign xor_1_out = in_1 ^ in_2;  // XOR_Gate xor_1, 32 bits wide

  // Notes on the sheet:
  //   00 = AND
  //   01 == OR
  //   11 XOR
  //   10 = NOR
  //   May Implement Later for smaller ALU
endmodule

module R_Zero (
  input  [31:0] in_1,
  output out_2
);

  wire or_1_out;

  or or_1 (or_1_out, in_1[31], in_1[30], in_1[29], in_1[28], in_1[27], in_1[26], in_1[25], in_1[24], in_1[23], in_1[22], in_1[21], in_1[20], in_1[19], in_1[18], in_1[17], in_1[16], in_1[15], in_1[14], in_1[13], in_1[12], in_1[11], in_1[10], in_1[9], in_1[8], in_1[7], in_1[6], in_1[5], in_1[4], in_1[3], in_1[2], in_1[1], in_1[0]);
  not not_1 (out_2, or_1_out);
endmodule

// Constant 1
module _2_s_Complement (
  input  [31:0] A,
  output [31:0] out_2
);

  wire [31:0] _32B_NOT_not_32b;

  NOT_32 _32B_NOT (._32B_in(A), .NOT_32B(_32B_NOT_not_32b));
  Adder #(.width(32)) adder_1 (.a(_32B_NOT_not_32b), .b(32'h1), .out(out_2));  // open: cin, cout
endmodule

module Shift_Right (
  input  [31:0] Input,
  input  in_2,
  input  in_3,
  input  in_4,
  input  in_5,
  input  in_6,
  input  in_7,
  output [31:0] OUTPUT
);

  wire multiplexer_1_out, multiplexer_2_out, multiplexer_3_out, multiplexer_4_out, multiplexer_5_out,
       multiplexer_6_out, multiplexer_7_out, multiplexer_8_out, multiplexer_9_out, multiplexer_10_out,
       multiplexer_11_out, multiplexer_12_out, multiplexer_15_out, multiplexer_16_out, multiplexer_17_out,
       multiplexer_18_out, multiplexer_19_out, multiplexer_20_out, multiplexer_21_out, multiplexer_22_out,
       multiplexer_25_out, multiplexer_26_out, multiplexer_27_out, multiplexer_28_out, multiplexer_29_out,
       multiplexer_30_out, multiplexer_31_out, multiplexer_32_out, multiplexer_35_out, multiplexer_36_out,
       multiplexer_37_out, multiplexer_38_out, multiplexer_39_out, multiplexer_40_out, multiplexer_41_out,
       multiplexer_42_out, multiplexer_45_out, multiplexer_46_out, multiplexer_47_out, multiplexer_48_out,
       multiplexer_49_out, multiplexer_50_out, multiplexer_51_out, multiplexer_52_out, multiplexer_55_out,
       multiplexer_56_out, multiplexer_57_out, multiplexer_58_out, multiplexer_59_out, multiplexer_60_out,
       multiplexer_61_out, multiplexer_62_out, multiplexer_65_out, multiplexer_66_out, multiplexer_67_out,
       multiplexer_68_out, multiplexer_69_out, multiplexer_70_out, multiplexer_71_out, multiplexer_72_out,
       multiplexer_75_out, multiplexer_76_out, multiplexer_77_out, multiplexer_78_out, multiplexer_79_out,
       multiplexer_80_out, multiplexer_81_out, multiplexer_82_out, multiplexer_85_out, multiplexer_86_out,
       multiplexer_87_out, multiplexer_88_out, multiplexer_89_out, multiplexer_90_out, multiplexer_91_out,
       multiplexer_92_out, multiplexer_95_out, multiplexer_96_out, multiplexer_97_out, multiplexer_98_out,
       multiplexer_99_out, multiplexer_100_out, multiplexer_101_out, multiplexer_102_out,
       multiplexer_105_out, multiplexer_106_out, multiplexer_107_out, multiplexer_108_out,
       multiplexer_109_out, multiplexer_110_out, multiplexer_111_out, multiplexer_112_out,
       multiplexer_115_out, multiplexer_116_out, multiplexer_117_out, multiplexer_118_out,
       multiplexer_119_out, multiplexer_120_out, multiplexer_121_out, multiplexer_122_out,
       multiplexer_125_out, multiplexer_126_out, multiplexer_127_out, multiplexer_128_out,
       multiplexer_129_out, multiplexer_130_out, multiplexer_131_out, multiplexer_132_out,
       multiplexer_135_out, multiplexer_136_out, multiplexer_137_out, multiplexer_138_out,
       multiplexer_139_out, multiplexer_140_out, multiplexer_141_out, multiplexer_142_out,
       multiplexer_145_out, multiplexer_146_out, multiplexer_147_out, multiplexer_148_out,
       multiplexer_149_out, multiplexer_150_out, multiplexer_151_out, multiplexer_152_out,
       multiplexer_155_out, multiplexer_156_out, multiplexer_157_out, multiplexer_158_out,
       multiplexer_159_out;

  Multiplexer multiplexer_1 (.in0(1'b0), .in1(Input[31]), .out(multiplexer_1_out), .sel(in_2));  // open: en
  Multiplexer multiplexer_2 (
    .in0(Input[31]), .in1(multiplexer_1_out), .out(multiplexer_2_out), .sel(in_3));  // open: en
  Multiplexer multiplexer_3 (
    .in0(multiplexer_2_out), .in1(multiplexer_1_out), .out(multiplexer_3_out), .sel(in_4));  // open: en
  Multiplexer multiplexer_4 (
    .in0(multiplexer_3_out), .in1(multiplexer_1_out), .out(multiplexer_4_out), .sel(in_5));  // open: en
  Multiplexer multiplexer_5 (
    .in0(Input[30]), .in1(multiplexer_1_out), .out(multiplexer_5_out), .sel(in_3));  // open: en
  Multiplexer multiplexer_6 (
    .in0(Input[29]), .in1(multiplexer_1_out), .out(multiplexer_6_out), .sel(in_3));  // open: en
  Multiplexer multiplexer_7 (
    .in0(multiplexer_5_out), .in1(multiplexer_1_out), .out(multiplexer_7_out), .sel(in_4));  // open: en
  Multiplexer multiplexer_8 (
    .in0(multiplexer_6_out), .in1(multiplexer_1_out), .out(multiplexer_8_out), .sel(in_4));  // open: en
  Multiplexer multiplexer_9 (
    .in0(multiplexer_8_out), .in1(multiplexer_1_out), .out(multiplexer_9_out), .sel(in_5));  // open: en
  Multiplexer multiplexer_10 (
    .in0(multiplexer_7_out), .in1(multiplexer_1_out), .out(multiplexer_10_out), .sel(in_5));  // open: en
  Multiplexer multiplexer_11 (
    .in0(multiplexer_4_out), .in1(multiplexer_1_out), .out(multiplexer_11_out), .sel(in_6));  // open: en
  Multiplexer multiplexer_12 (
    .in0(multiplexer_10_out), .in1(multiplexer_1_out), .out(multiplexer_12_out), .sel(in_6));  // open: en
  Multiplexer multiplexer_13 (
    .in0(multiplexer_11_out), .in1(multiplexer_1_out), .out(OUTPUT[31]), .sel(in_7));  // open: en
  Multiplexer multiplexer_14 (
    .in0(multiplexer_12_out), .in1(multiplexer_11_out), .out(OUTPUT[30]), .sel(in_7));  // open: en
  Multiplexer multiplexer_15 (
    .in0(Input[27]), .in1(multiplexer_1_out), .out(multiplexer_15_out), .sel(in_3));  // open: en
  Multiplexer multiplexer_16 (
    .in0(Input[28]), .in1(multiplexer_1_out), .out(multiplexer_16_out), .sel(in_3));  // open: en
  Multiplexer multiplexer_17 (
    .in0(multiplexer_15_out), .in1(multiplexer_1_out), .out(multiplexer_17_out), .sel(in_4));  // open: en
  Multiplexer multiplexer_18 (
    .in0(multiplexer_16_out), .in1(multiplexer_1_out), .out(multiplexer_18_out), .sel(in_4));  // open: en
  Multiplexer multiplexer_19 (
    .in0(multiplexer_18_out), .in1(multiplexer_1_out), .out(multiplexer_19_out), .sel(in_5));  // open: en
  Multiplexer multiplexer_20 (
    .in0(multiplexer_17_out), .in1(multiplexer_3_out), .out(multiplexer_20_out), .sel(in_5));  // open: en
  Multiplexer multiplexer_21 (
    .in0(multiplexer_19_out), .in1(multiplexer_10_out), .out(multiplexer_21_out), .sel(in_6));  // open: en
  Multiplexer multiplexer_22 (
    .in0(multiplexer_9_out), .in1(multiplexer_4_out), .out(multiplexer_22_out), .sel(in_6));  // open: en
  Multiplexer multiplexer_23 (
    .in0(multiplexer_21_out), .in1(multiplexer_22_out), .out(OUTPUT[28]), .sel(in_7));  // open: en
  Multiplexer multiplexer_24 (
    .in0(multiplexer_22_out), .in1(multiplexer_12_out), .out(OUTPUT[29]), .sel(in_7));  // open: en
  Multiplexer multiplexer_25 (
    .in0(Input[25]), .in1(multiplexer_1_out), .out(multiplexer_25_out), .sel(in_3));  // open: en
  Multiplexer multiplexer_26 (
    .in0(Input[26]), .in1(multiplexer_1_out), .out(multiplexer_26_out), .sel(in_3));  // open: en
  Multiplexer multiplexer_27 (
    .in0(multiplexer_26_out), .in1(multiplexer_1_out), .out(multiplexer_27_out), .sel(in_4));  // open: en
  Multiplexer multiplexer_28 (
    .in0(multiplexer_25_out), .in1(multiplexer_1_out), .out(multiplexer_28_out), .sel(in_4));  // open: en
  Multiplexer multiplexer_29 (
    .in0(multiplexer_27_out), .in1(multiplexer_7_out), .out(multiplexer_29_out), .sel(in_5));  // open: en
  Multiplexer multiplexer_30 (
    .in0(multiplexer_28_out), .in1(multiplexer_8_out), .out(multiplexer_30_out), .sel(in_5));  // open: en
  Multiplexer multiplexer_31 (
    .in0(multiplexer_29_out), .in1(multiplexer_19_out), .out(multiplexer_31_out), .sel(in_6));  // open: en
  Multiplexer multiplexer_32 (
    .in0(multiplexer_20_out), .in1(multiplexer_9_out), .out(multiplexer_32_out), .sel(in_6));  // open: en
  Multiplexer multiplexer_33 (
    .in0(multiplexer_32_out), .in1(multiplexer_21_out), .out(OUTPUT[27]), .sel(in_7));  // open: en
  Multiplexer multiplexer_34 (
    .in0(multiplexer_31_out), .in1(multiplexer_32_out), .out(OUTPUT[26]), .sel(in_7));  // open: en
  Multiplexer multiplexer_35 (
    .in0(Input[24]), .in1(multiplexer_1_out), .out(multiplexer_35_out), .sel(in_3));  // open: en
  Multiplexer multiplexer_36 (
    .in0(Input[23]), .in1(multiplexer_1_out), .out(multiplexer_36_out), .sel(in_3));  // open: en
  Multiplexer multiplexer_37 (
    .in0(multiplexer_35_out), .in1(multiplexer_1_out), .out(multiplexer_37_out), .sel(in_4));  // open: en
  Multiplexer multiplexer_38 (
    .in0(multiplexer_36_out), .in1(multiplexer_2_out), .out(multiplexer_38_out), .sel(in_4));  // open: en
  Multiplexer multiplexer_39 (
    .in0(multiplexer_38_out), .in1(multiplexer_17_out), .out(multiplexer_39_out), .sel(in_5));  // open: en
  Multiplexer multiplexer_40 (
    .in0(multiplexer_37_out), .in1(multiplexer_18_out), .out(multiplexer_40_out), .sel(in_5));  // open: en
  Multiplexer multiplexer_41 (
    .in0(multiplexer_30_out), .in1(multiplexer_20_out), .out(multiplexer_41_out), .sel(in_6));  // open: en
  Multiplexer multiplexer_42 (
    .in0(multiplexer_40_out), .in1(multiplexer_29_out), .out(multiplexer_42_out), .sel(in_6));  // open: en
  Multiplexer multiplexer_43 (
    .in0(multiplexer_42_out), .in1(multiplexer_41_out), .out(OUTPUT[24]), .sel(in_7));  // open: en
  Multiplexer multiplexer_44 (
    .in0(multiplexer_41_out), .in1(multiplexer_31_out), .out(OUTPUT[25]), .sel(in_7));  // open: en
  Multiplexer multiplexer_45 (
    .in0(Input[21]), .in1(multiplexer_1_out), .out(multiplexer_45_out), .sel(in_3));  // open: en
  Multiplexer multiplexer_46 (
    .in0(Input[22]), .in1(multiplexer_1_out), .out(multiplexer_46_out), .sel(in_3));  // open: en
  Multiplexer multiplexer_47 (
    .in0(multiplexer_45_out), .in1(multiplexer_6_out), .out(multiplexer_47_out), .sel(in_4));  // open: en
  Multiplexer multiplexer_48 (
    .in0(multiplexer_46_out), .in1(multiplexer_5_out), .out(multiplexer_48_out), .sel(in_4));  // open: en
  Multiplexer multiplexer_49 (
    .in0(multiplexer_47_out), .in1(multiplexer_28_out), .out(multiplexer_49_out), .sel(in_5));  // open: en
  Multiplexer multiplexer_50 (
    .in0(multiplexer_48_out), .in1(multiplexer_27_out), .out(multiplexer_50_out), .sel(in_5));  // open: en
  Multiplexer multiplexer_51 (
    .in0(multiplexer_50_out), .in1(multiplexer_40_out), .out(multiplexer_51_out), .sel(in_6));  // open: en
  Multiplexer multiplexer_52 (
    .in0(multiplexer_39_out), .in1(multiplexer_30_out), .out(multiplexer_52_out), .sel(in_6));  // open: en
  Multiplexer multiplexer_53 (
    .in0(multiplexer_52_out), .in1(multiplexer_42_out), .out(OUTPUT[23]), .sel(in_7));  // open: en
  Multiplexer multiplexer_54 (
    .in0(multiplexer_51_out), .in1(multiplexer_52_out), .out(OUTPUT[22]), .sel(in_7));  // open: en
  Multiplexer multiplexer_55 (
    .in0(Input[19]), .in1(multiplexer_1_out), .out(multiplexer_55_out), .sel(in_3));  // open: en
  Multiplexer multiplexer_56 (
    .in0(Input[20]), .in1(multiplexer_1_out), .out(multiplexer_56_out), .sel(in_3));  // open: en
  Multiplexer multiplexer_57 (
    .in0(multiplexer_56_out), .in1(multiplexer_16_out), .out(multiplexer_57_out), .sel(in_4));  // open: en
  Multiplexer multiplexer_58 (
    .in0(multiplexer_55_out), .in1(multiplexer_15_out), .out(multiplexer_58_out), .sel(in_4));  // open: en
  Multiplexer multiplexer_59 (
    .in0(multiplexer_57_out), .in1(multiplexer_37_out), .out(multiplexer_59_out), .sel(in_5));  // open: en
  Multiplexer multiplexer_60 (
    .in0(multiplexer_58_out), .in1(multiplexer_38_out), .out(multiplexer_60_out), .sel(in_5));  // open: en
  Multiplexer multiplexer_61 (
    .in0(multiplexer_59_out), .in1(multiplexer_50_out), .out(multiplexer_61_out), .sel(in_6));  // open: en
  Multiplexer multiplexer_62 (
    .in0(multiplexer_49_out), .in1(multiplexer_39_out), .out(multiplexer_62_out), .sel(in_6));  // open: en
  Multiplexer multiplexer_63 (
    .in0(multiplexer_61_out), .in1(multiplexer_62_out), .out(OUTPUT[20]), .sel(in_7));  // open: en
  Multiplexer multiplexer_64 (
    .in0(multiplexer_62_out), .in1(multiplexer_51_out), .out(OUTPUT[21]), .sel(in_7));  // open: en
  Multiplexer multiplexer_65 (
    .in0(Input[17]), .in1(multiplexer_1_out), .out(multiplexer_65_out), .sel(in_3));  // open: en
  Multiplexer multiplexer_66 (
    .in0(Input[18]), .in1(multiplexer_1_out), .out(multiplexer_66_out), .sel(in_3));  // open: en
  Multiplexer multiplexer_67 (
    .in0(multiplexer_66_out), .in1(multiplexer_26_out), .out(multiplexer_67_out), .sel(in_4));  // open: en
  Multiplexer multiplexer_68 (
    .in0(multiplexer_65_out), .in1(multiplexer_25_out), .out(multiplexer_68_out), .sel(in_4));  // open: en
  Multiplexer multiplexer_69 (
    .in0(multiplexer_67_out), .in1(multiplexer_48_out), .out(multiplexer_69_out), .sel(in_5));  // open: en
  Multiplexer multiplexer_70 (
    .in0(multiplexer_68_out), .in1(multiplexer_47_out), .out(multiplexer_70_out), .sel(in_5));  // open: en
  Multiplexer multiplexer_71 (
    .in0(multiplexer_60_out), .in1(multiplexer_49_out), .out(multiplexer_71_out), .sel(in_6));  // open: en
  Multiplexer multiplexer_72 (
    .in0(multiplexer_69_out), .in1(multiplexer_59_out), .out(multiplexer_72_out), .sel(in_6));  // open: en
  Multiplexer multiplexer_73 (
    .in0(multiplexer_71_out), .in1(multiplexer_61_out), .out(OUTPUT[19]), .sel(in_7));  // open: en
  Multiplexer multiplexer_74 (
    .in0(multiplexer_72_out), .in1(multiplexer_71_out), .out(OUTPUT[18]), .sel(in_7));  // open: en
  Multiplexer multiplexer_75 (.in0(Input[15]), .in1(Input[31]), .out(multiplexer_75_out), .sel(in_3));  // open: en
  Multiplexer multiplexer_76 (
    .in0(Input[16]), .in1(multiplexer_1_out), .out(multiplexer_76_out), .sel(in_3));  // open: en
  Multiplexer multiplexer_77 (
    .in0(multiplexer_75_out), .in1(multiplexer_36_out), .out(multiplexer_77_out), .sel(in_4));  // open: en
  Multiplexer multiplexer_78 (
    .in0(multiplexer_76_out), .in1(multiplexer_35_out), .out(multiplexer_78_out), .sel(in_4));  // open: en
  Multiplexer multiplexer_79 (
    .in0(multiplexer_77_out), .in1(multiplexer_58_out), .out(multiplexer_79_out), .sel(in_5));  // open: en
  Multiplexer multiplexer_80 (
    .in0(multiplexer_78_out), .in1(multiplexer_57_out), .out(multiplexer_80_out), .sel(in_5));  // open: en
  Multiplexer multiplexer_81 (
    .in0(multiplexer_70_out), .in1(multiplexer_60_out), .out(multiplexer_81_out), .sel(in_6));  // open: en
  Multiplexer multiplexer_82 (
    .in0(multiplexer_80_out), .in1(multiplexer_69_out), .out(multiplexer_82_out), .sel(in_6));  // open: en
  Multiplexer multiplexer_83 (
    .in0(multiplexer_81_out), .in1(multiplexer_72_out), .out(OUTPUT[17]), .sel(in_7));  // open: en
  Multiplexer multiplexer_84 (
    .in0(multiplexer_82_out), .in1(multiplexer_81_out), .out(OUTPUT[16]), .sel(in_7));  // open: en
  Multiplexer multiplexer_85 (.in0(Input[13]), .in1(Input[29]), .out(multiplexer_85_out), .sel(in_3));  // open: en
  Multiplexer multiplexer_86 (.in0(Input[14]), .in1(Input[30]), .out(multiplexer_86_out), .sel(in_3));  // open: en
  Multiplexer multiplexer_87 (
    .in0(multiplexer_86_out), .in1(multiplexer_46_out), .out(multiplexer_87_out), .sel(in_4));  // open: en
  Multiplexer multiplexer_88 (
    .in0(multiplexer_85_out), .in1(multiplexer_45_out), .out(multiplexer_88_out), .sel(in_4));  // open: en
  Multiplexer multiplexer_89 (
    .in0(multiplexer_88_out), .in1(multiplexer_68_out), .out(multiplexer_89_out), .sel(in_5));  // open: en
  Multiplexer multiplexer_90 (
    .in0(multiplexer_87_out), .in1(multiplexer_67_out), .out(multiplexer_90_out), .sel(in_5));  // open: en
  Multiplexer multiplexer_91 (
    .in0(multiplexer_90_out), .in1(multiplexer_80_out), .out(multiplexer_91_out), .sel(in_6));  // open: en
  Multiplexer multiplexer_92 (
    .in0(multiplexer_79_out), .in1(multiplexer_70_out), .out(multiplexer_92_out), .sel(in_6));  // open: en
  Multiplexer multiplexer_93 (
    .in0(multiplexer_91_out), .in1(multiplexer_92_out), .out(OUTPUT[14]), .sel(in_7));  // open: en
  Multiplexer multiplexer_94 (
    .in0(multiplexer_92_out), .in1(multiplexer_82_out), .out(OUTPUT[15]), .sel(in_7));  // open: en
  Multiplexer multiplexer_95 (.in0(Input[11]), .in1(Input[27]), .out(multiplexer_95_out), .sel(in_3));  // open: en
  Multiplexer multiplexer_96 (.in0(Input[12]), .in1(Input[28]), .out(multiplexer_96_out), .sel(in_3));  // open: en
  Multiplexer multiplexer_97 (
    .in0(multiplexer_96_out), .in1(multiplexer_56_out), .out(multiplexer_97_out), .sel(in_4));  // open: en
  Multiplexer multiplexer_98 (
    .in0(multiplexer_95_out), .in1(multiplexer_55_out), .out(multiplexer_98_out), .sel(in_4));  // open: en
  Multiplexer multiplexer_99 (
    .in0(multiplexer_98_out), .in1(multiplexer_77_out), .out(multiplexer_99_out), .sel(in_5));  // open: en
  Multiplexer multiplexer_100 (
    .in0(multiplexer_97_out), .in1(multiplexer_78_out), .out(multiplexer_100_out), .sel(in_5));  // open: en
  Multiplexer multiplexer_101 (
    .in0(multiplexer_100_out), .in1(multiplexer_90_out), .out(multiplexer_101_out), .sel(in_6));  // open: en
  Multiplexer multiplexer_102 (
    .in0(multiplexer_89_out), .in1(multiplexer_79_out), .out(multiplexer_102_out), .sel(in_6));  // open: en
  Multiplexer multiplexer_103 (
    .in0(multiplexer_101_out), .in1(multiplexer_102_out), .out(OUTPUT[12]), .sel(in_7));  // open: en
  Multiplexer multiplexer_104 (
    .in0(multiplexer_102_out), .in1(multiplexer_91_out), .out(OUTPUT[13]), .sel(in_7));  // open: en
  Multiplexer multiplexer_105 (.in0(Input[9]), .in1(Input[25]), .out(multiplexer_105_out), .sel(in_3));  // open: en
  Multiplexer multiplexer_106 (.in0(Input[10]), .in1(Input[26]), .out(multiplexer_106_out), .sel(in_3));  // open: en
  Multiplexer multiplexer_107 (
    .in0(multiplexer_106_out), .in1(multiplexer_66_out), .out(multiplexer_107_out), .sel(in_4));  // open: en
  Multiplexer multiplexer_108 (
    .in0(multiplexer_105_out), .in1(multiplexer_65_out), .out(multiplexer_108_out), .sel(in_4));  // open: en
  Multiplexer multiplexer_109 (
    .in0(multiplexer_108_out), .in1(multiplexer_88_out), .out(multiplexer_109_out), .sel(in_5));  // open: en
  Multiplexer multiplexer_110 (
    .in0(multiplexer_107_out), .in1(multiplexer_87_out), .out(multiplexer_110_out), .sel(in_5));  // open: en
  Multiplexer multiplexer_111 (
    .in0(multiplexer_99_out), .in1(multiplexer_89_out), .out(multiplexer_111_out), .sel(in_6));  // open: en
  Multiplexer multiplexer_112 (
    .in0(multiplexer_110_out), .in1(multiplexer_100_out), .out(multiplexer_112_out), .sel(in_6));  // open: en
  Multiplexer multiplexer_113 (
    .in0(multiplexer_111_out), .in1(multiplexer_101_out), .out(OUTPUT[11]), .sel(in_7));  // open: en
  Multiplexer multiplexer_114 (
    .in0(multiplexer_112_out), .in1(multiplexer_111_out), .out(OUTPUT[10]), .sel(in_7));  // open: en
  Multiplexer multiplexer_115 (.in0(Input[7]), .in1(Input[23]), .out(multiplexer_115_out), .sel(in_3));  // open: en
  Multiplexer multiplexer_116 (.in0(Input[8]), .in1(Input[24]), .out(multiplexer_116_out), .sel(in_3));  // open: en
  Multiplexer multiplexer_117 (
    .in0(multiplexer_115_out), .in1(multiplexer_75_out), .out(multiplexer_117_out), .sel(in_4));  // open: en
  Multiplexer multiplexer_118 (
    .in0(multiplexer_116_out), .in1(multiplexer_76_out), .out(multiplexer_118_out), .sel(in_4));  // open: en
  Multiplexer multiplexer_119 (
    .in0(multiplexer_117_out), .in1(multiplexer_98_out), .out(multiplexer_119_out), .sel(in_5));  // open: en
  Multiplexer multiplexer_120 (
    .in0(multiplexer_118_out), .in1(multiplexer_97_out), .out(multiplexer_120_out), .sel(in_5));  // open: en
  Multiplexer multiplexer_121 (
    .in0(multiplexer_109_out), .in1(multiplexer_99_out), .out(multiplexer_121_out), .sel(in_6));  // open: en
  Multiplexer multiplexer_122 (
    .in0(multiplexer_120_out), .in1(multiplexer_110_out), .out(multiplexer_122_out), .sel(in_6));  // open: en
  Multiplexer multiplexer_123 (
    .in0(multiplexer_121_out), .in1(multiplexer_112_out), .out(OUTPUT[9]), .sel(in_7));  // open: en
  Multiplexer multiplexer_124 (
    .in0(multiplexer_122_out), .in1(multiplexer_121_out), .out(OUTPUT[8]), .sel(in_7));  // open: en
  Multiplexer multiplexer_125 (.in0(Input[5]), .in1(Input[21]), .out(multiplexer_125_out), .sel(in_3));  // open: en
  Multiplexer multiplexer_126 (.in0(Input[6]), .in1(Input[22]), .out(multiplexer_126_out), .sel(in_3));  // open: en
  Multiplexer multiplexer_127 (
    .in0(multiplexer_125_out), .in1(multiplexer_85_out), .out(multiplexer_127_out), .sel(in_4));  // open: en
  Multiplexer multiplexer_128 (
    .in0(multiplexer_126_out), .in1(multiplexer_86_out), .out(multiplexer_128_out), .sel(in_4));  // open: en
  Multiplexer multiplexer_129 (
    .in0(multiplexer_128_out), .in1(multiplexer_107_out), .out(multiplexer_129_out), .sel(in_5));  // open: en
  Multiplexer multiplexer_130 (
    .in0(multiplexer_127_out), .in1(multiplexer_108_out), .out(multiplexer_130_out), .sel(in_5));  // open: en
  Multiplexer multiplexer_131 (
    .in0(multiplexer_119_out), .in1(multiplexer_109_out), .out(multiplexer_131_out), .sel(in_6));  // open: en
  Multiplexer multiplexer_132 (
    .in0(multiplexer_129_out), .in1(multiplexer_120_out), .out(multiplexer_132_out), .sel(in_6));  // open: en
  Multiplexer multiplexer_133 (
    .in0(multiplexer_131_out), .in1(multiplexer_122_out), .out(OUTPUT[7]), .sel(in_7));  // open: en
  Multiplexer multiplexer_134 (
    .in0(multiplexer_132_out), .in1(multiplexer_131_out), .out(OUTPUT[6]), .sel(in_7));  // open: en
  Multiplexer multiplexer_135 (.in0(Input[3]), .in1(Input[19]), .out(multiplexer_135_out), .sel(in_3));  // open: en
  Multiplexer multiplexer_136 (.in0(Input[4]), .in1(Input[20]), .out(multiplexer_136_out), .sel(in_3));  // open: en
  Multiplexer multiplexer_137 (
    .in0(multiplexer_136_out), .in1(multiplexer_96_out), .out(multiplexer_137_out), .sel(in_4));  // open: en
  Multiplexer multiplexer_138 (
    .in0(multiplexer_135_out), .in1(multiplexer_95_out), .out(multiplexer_138_out), .sel(in_4));  // open: en
  Multiplexer multiplexer_139 (
    .in0(multiplexer_137_out), .in1(multiplexer_118_out), .out(multiplexer_139_out), .sel(in_5));  // open: en
  Multiplexer multiplexer_140 (
    .in0(multiplexer_138_out), .in1(multiplexer_117_out), .out(multiplexer_140_out), .sel(in_5));  // open: en
  Multiplexer multiplexer_141 (
    .in0(multiplexer_130_out), .in1(multiplexer_119_out), .out(multiplexer_141_out), .sel(in_6));  // open: en
  Multiplexer multiplexer_142 (
    .in0(multiplexer_139_out), .in1(multiplexer_129_out), .out(multiplexer_142_out), .sel(in_6));  // open: en
  Multiplexer multiplexer_143 (
    .in0(multiplexer_141_out), .in1(multiplexer_132_out), .out(OUTPUT[5]), .sel(in_7));  // open: en
  Multiplexer multiplexer_144 (
    .in0(multiplexer_142_out), .in1(multiplexer_141_out), .out(OUTPUT[4]), .sel(in_7));  // open: en
  Multiplexer multiplexer_145 (.in0(Input[2]), .in1(Input[18]), .out(multiplexer_145_out), .sel(in_3));  // open: en
  Multiplexer multiplexer_146 (.in0(Input[1]), .in1(Input[17]), .out(multiplexer_146_out), .sel(in_3));  // open: en
  Multiplexer multiplexer_147 (
    .in0(multiplexer_146_out), .in1(multiplexer_105_out), .out(multiplexer_147_out), .sel(in_4));  // open: en
  Multiplexer multiplexer_148 (
    .in0(multiplexer_145_out), .in1(multiplexer_106_out), .out(multiplexer_148_out), .sel(in_4));  // open: en
  Multiplexer multiplexer_149 (
    .in0(multiplexer_148_out), .in1(multiplexer_128_out), .out(multiplexer_149_out), .sel(in_5));  // open: en
  Multiplexer multiplexer_150 (
    .in0(multiplexer_147_out), .in1(multiplexer_127_out), .out(multiplexer_150_out), .sel(in_5));  // open: en
  Multiplexer multiplexer_151 (
    .in0(multiplexer_149_out), .in1(multiplexer_139_out), .out(multiplexer_151_out), .sel(in_6));  // open: en
  Multiplexer multiplexer_152 (
    .in0(multiplexer_140_out), .in1(multiplexer_130_out), .out(multiplexer_152_out), .sel(in_6));  // open: en
  Multiplexer multiplexer_153 (
    .in0(multiplexer_152_out), .in1(multiplexer_142_out), .out(OUTPUT[3]), .sel(in_7));  // open: en
  Multiplexer multiplexer_154 (
    .in0(multiplexer_151_out), .in1(multiplexer_152_out), .out(OUTPUT[2]), .sel(in_7));  // open: en
  Multiplexer multiplexer_155 (.in0(Input[0]), .in1(Input[16]), .out(multiplexer_155_out), .sel(in_3));  // open: en
  Multiplexer multiplexer_156 (
    .in0(multiplexer_155_out), .in1(multiplexer_116_out), .out(multiplexer_156_out), .sel(in_4));  // open: en
  Multiplexer multiplexer_157 (
    .in0(multiplexer_156_out), .in1(multiplexer_137_out), .out(multiplexer_157_out), .sel(in_5));  // open: en
  Multiplexer multiplexer_158 (
    .in0(multiplexer_157_out), .in1(multiplexer_149_out), .out(multiplexer_158_out), .sel(in_6));  // open: en
  Multiplexer multiplexer_159 (
    .in0(multiplexer_150_out), .in1(multiplexer_140_out), .out(multiplexer_159_out), .sel(in_6));  // open: en
  Multiplexer multiplexer_160 (
    .in0(multiplexer_159_out), .in1(multiplexer_151_out), .out(OUTPUT[1]), .sel(in_7));  // open: en
  Multiplexer multiplexer_161 (
    .in0(multiplexer_158_out), .in1(multiplexer_159_out), .out(OUTPUT[0]), .sel(in_7));  // open: en
endmodule

module Shift_Left (
  input  [31:0] Input,
  input  in_2,
  input  in_3,
  input  in_4,
  input  in_5,
  input  in_6,
  output [31:0] OUTPUT
);

  wire multiplexer_1_out, multiplexer_2_out, multiplexer_3_out, multiplexer_4_out, multiplexer_5_out,
       multiplexer_6_out, multiplexer_7_out, multiplexer_8_out, multiplexer_9_out, multiplexer_10_out,
       multiplexer_11_out, multiplexer_14_out, multiplexer_15_out, multiplexer_16_out, multiplexer_17_out,
       multiplexer_18_out, multiplexer_19_out, multiplexer_20_out, multiplexer_21_out, multiplexer_24_out,
       multiplexer_25_out, multiplexer_26_out, multiplexer_27_out, multiplexer_28_out, multiplexer_29_out,
       multiplexer_30_out, multiplexer_31_out, multiplexer_34_out, multiplexer_35_out, multiplexer_36_out,
       multiplexer_37_out, multiplexer_38_out, multiplexer_39_out, multiplexer_40_out, multiplexer_41_out,
       multiplexer_44_out, multiplexer_45_out, multiplexer_46_out, multiplexer_47_out, multiplexer_48_out,
       multiplexer_49_out, multiplexer_50_out, multiplexer_51_out, multiplexer_54_out, multiplexer_55_out,
       multiplexer_56_out, multiplexer_57_out, multiplexer_58_out, multiplexer_59_out, multiplexer_60_out,
       multiplexer_61_out, multiplexer_64_out, multiplexer_65_out, multiplexer_66_out, multiplexer_67_out,
       multiplexer_68_out, multiplexer_69_out, multiplexer_70_out, multiplexer_71_out, multiplexer_74_out,
       multiplexer_75_out, multiplexer_76_out, multiplexer_77_out, multiplexer_78_out, multiplexer_79_out,
       multiplexer_80_out, multiplexer_81_out, multiplexer_84_out, multiplexer_85_out, multiplexer_86_out,
       multiplexer_87_out, multiplexer_88_out, multiplexer_89_out, multiplexer_90_out, multiplexer_91_out,
       multiplexer_94_out, multiplexer_95_out, multiplexer_96_out, multiplexer_97_out, multiplexer_98_out,
       multiplexer_99_out, multiplexer_100_out, multiplexer_101_out, multiplexer_104_out,
       multiplexer_105_out, multiplexer_106_out, multiplexer_107_out, multiplexer_108_out,
       multiplexer_109_out, multiplexer_110_out, multiplexer_111_out, multiplexer_114_out,
       multiplexer_115_out, multiplexer_116_out, multiplexer_117_out, multiplexer_118_out,
       multiplexer_119_out, multiplexer_120_out, multiplexer_121_out, multiplexer_124_out,
       multiplexer_125_out, multiplexer_126_out, multiplexer_127_out, multiplexer_128_out,
       multiplexer_129_out, multiplexer_130_out, multiplexer_131_out, multiplexer_134_out,
       multiplexer_135_out, multiplexer_136_out, multiplexer_137_out, multiplexer_138_out,
       multiplexer_139_out, multiplexer_140_out, multiplexer_141_out, multiplexer_144_out,
       multiplexer_145_out, multiplexer_146_out, multiplexer_147_out, multiplexer_148_out,
       multiplexer_149_out, multiplexer_150_out, multiplexer_151_out, multiplexer_154_out,
       multiplexer_155_out, multiplexer_156_out, multiplexer_157_out, multiplexer_158_out;

  Multiplexer multiplexer_1 (.in0(Input[0]), .in1(1'b0), .out(multiplexer_1_out), .sel(in_2));  // open: en
  Multiplexer multiplexer_2 (.in0(multiplexer_1_out), .in1(1'b0), .out(multiplexer_2_out), .sel(in_3));  // open: en
  Multiplexer multiplexer_3 (.in0(multiplexer_2_out), .in1(1'b0), .out(multiplexer_3_out), .sel(in_4));  // open: en
  Multiplexer multiplexer_4 (.in0(Input[2]), .in1(1'b0), .out(multiplexer_4_out), .sel(in_2));  // open: en
  Multiplexer multiplexer_5 (.in0(Input[1]), .in1(1'b0), .out(multiplexer_5_out), .sel(in_2));  // open: en
  Multiplexer multiplexer_6 (.in0(multiplexer_4_out), .in1(1'b0), .out(multiplexer_6_out), .sel(in_3));  // open: en
  Multiplexer multiplexer_7 (.in0(multiplexer_5_out), .in1(1'b0), .out(multiplexer_7_out), .sel(in_3));  // open: en
  Multiplexer multiplexer_8 (.in0(multiplexer_7_out), .in1(1'b0), .out(multiplexer_8_out), .sel(in_4));  // open: en
  Multiplexer multiplexer_9 (.in0(multiplexer_6_out), .in1(1'b0), .out(multiplexer_9_out), .sel(in_4));  // open: en
  Multiplexer multiplexer_10 (.in0(multiplexer_3_out), .in1(1'b0), .out(multiplexer_10_out), .sel(in_5));  // open: en
  Multiplexer multiplexer_11 (.in0(multiplexer_8_out), .in1(1'b0), .out(multiplexer_11_out), .sel(in_5));  // open: en
  Multiplexer multiplexer_12 (
    .in0(multiplexer_11_out), .in1(multiplexer_10_out), .out(OUTPUT[1]), .sel(in_6));  // open: en
  Multiplexer multiplexer_13 (.in0(multiplexer_10_out), .in1(1'b0), .out(OUTPUT[0]), .sel(in_6));  // open: en
  Multiplexer multiplexer_14 (.in0(Input[4]), .in1(1'b0), .out(multiplexer_14_out), .sel(in_2));  // open: en
  Multiplexer multiplexer_15 (.in0(Input[3]), .in1(1'b0), .out(multiplexer_15_out), .sel(in_2));  // open: en
  Multiplexer multiplexer_16 (.in0(multiplexer_14_out), .in1(1'b0), .out(multiplexer_16_out), .sel(in_3));  // open: en
  Multiplexer multiplexer_17 (.in0(multiplexer_15_out), .in1(1'b0), .out(multiplexer_17_out), .sel(in_3));  // open: en
  Multiplexer multiplexer_18 (.in0(multiplexer_17_out), .in1(1'b0), .out(multiplexer_18_out), .sel(in_4));  // open: en
  Multiplexer multiplexer_19 (
    .in0(multiplexer_16_out), .in1(multiplexer_2_out), .out(multiplexer_19_out), .sel(in_4));  // open: en
  Multiplexer multiplexer_20 (
    .in0(multiplexer_18_out), .in1(multiplexer_8_out), .out(multiplexer_20_out), .sel(in_5));  // open: en
  Multiplexer multiplexer_21 (
    .in0(multiplexer_9_out), .in1(multiplexer_3_out), .out(multiplexer_21_out), .sel(in_5));  // open: en
  Multiplexer multiplexer_22 (
    .in0(multiplexer_20_out), .in1(multiplexer_21_out), .out(OUTPUT[3]), .sel(in_6));  // open: en
  Multiplexer multiplexer_23 (
    .in0(multiplexer_21_out), .in1(multiplexer_11_out), .out(OUTPUT[2]), .sel(in_6));  // open: en
  Multiplexer multiplexer_24 (.in0(Input[5]), .in1(1'b0), .out(multiplexer_24_out), .sel(in_2));  // open: en
  Multiplexer multiplexer_25 (.in0(Input[6]), .in1(1'b0), .out(multiplexer_25_out), .sel(in_2));  // open: en
  Multiplexer multiplexer_26 (.in0(multiplexer_25_out), .in1(1'b0), .out(multiplexer_26_out), .sel(in_3));  // open: en
  Multiplexer multiplexer_27 (.in0(multiplexer_24_out), .in1(1'b0), .out(multiplexer_27_out), .sel(in_3));  // open: en
  Multiplexer multiplexer_28 (
    .in0(multiplexer_27_out), .in1(multiplexer_7_out), .out(multiplexer_28_out), .sel(in_4));  // open: en
  Multiplexer multiplexer_29 (
    .in0(multiplexer_26_out), .in1(multiplexer_6_out), .out(multiplexer_29_out), .sel(in_4));  // open: en
  Multiplexer multiplexer_30 (
    .in0(multiplexer_19_out), .in1(multiplexer_9_out), .out(multiplexer_30_out), .sel(in_5));  // open: en
  Multiplexer multiplexer_31 (
    .in0(multiplexer_28_out), .in1(multiplexer_18_out), .out(multiplexer_31_out), .sel(in_5));  // open: en
  Multiplexer multiplexer_32 (
    .in0(multiplexer_30_out), .in1(multiplexer_20_out), .out(OUTPUT[4]), .sel(in_6));  // open: en
  Multiplexer multiplexer_33 (
    .in0(multiplexer_31_out), .in1(multiplexer_30_out), .out(OUTPUT[5]), .sel(in_6));  // open: en
  Multiplexer multiplexer_34 (.in0(Input[8]), .in1(1'b0), .out(multiplexer_34_out), .sel(in_2));  // open: en
  Multiplexer multiplexer_35 (.in0(Input[7]), .in1(1'b0), .out(multiplexer_35_out), .sel(in_2));  // open: en
  Multiplexer multiplexer_36 (
    .in0(multiplexer_34_out), .in1(multiplexer_1_out), .out(multiplexer_36_out), .sel(in_3));  // open: en
  Multiplexer multiplexer_37 (.in0(multiplexer_35_out), .in1(1'b0), .out(multiplexer_37_out), .sel(in_3));  // open: en
  Multiplexer multiplexer_38 (
    .in0(multiplexer_36_out), .in1(multiplexer_16_out), .out(multiplexer_38_out), .sel(in_4));  // open: en
  Multiplexer multiplexer_39 (
    .in0(multiplexer_37_out), .in1(multiplexer_17_out), .out(multiplexer_39_out), .sel(in_4));  // open: en
  Multiplexer multiplexer_40 (
    .in0(multiplexer_39_out), .in1(multiplexer_28_out), .out(multiplexer_40_out), .sel(in_5));  // open: en
  Multiplexer multiplexer_41 (
    .in0(multiplexer_29_out), .in1(multiplexer_19_out), .out(multiplexer_41_out), .sel(in_5));  // open: en
  Multiplexer multiplexer_42 (
    .in0(multiplexer_41_out), .in1(multiplexer_31_out), .out(OUTPUT[6]), .sel(in_6));  // open: en
  Multiplexer multiplexer_43 (
    .in0(multiplexer_40_out), .in1(multiplexer_41_out), .out(OUTPUT[7]), .sel(in_6));  // open: en
  Multiplexer multiplexer_44 (.in0(Input[9]), .in1(1'b0), .out(multiplexer_44_out), .sel(in_2));  // open: en
  Multiplexer multiplexer_45 (.in0(Input[10]), .in1(1'b0), .out(multiplexer_45_out), .sel(in_2));  // open: en
  Multiplexer multiplexer_46 (
    .in0(multiplexer_45_out), .in1(multiplexer_4_out), .out(multiplexer_46_out), .sel(in_3));  // open: en
  Multiplexer multiplexer_47 (
    .in0(multiplexer_44_out), .in1(multiplexer_5_out), .out(multiplexer_47_out), .sel(in_3));  // open: en
  Multiplexer multiplexer_48 (
    .in0(multiplexer_47_out), .in1(multiplexer_27_out), .out(multiplexer_48_out), .sel(in_4));  // open: en
  Multiplexer multiplexer_49 (
    .in0(multiplexer_46_out), .in1(multiplexer_26_out), .out(multiplexer_49_out), .sel(in_4));  // open: en
  Multiplexer multiplexer_50 (
    .in0(multiplexer_38_out), .in1(multiplexer_29_out), .out(multiplexer_50_out), .sel(in_5));  // open: en
  Multiplexer multiplexer_51 (
    .in0(multiplexer_48_out), .in1(multiplexer_39_out), .out(multiplexer_51_out), .sel(in_5));  // open: en
  Multiplexer multiplexer_52 (
    .in0(multiplexer_50_out), .in1(multiplexer_40_out), .out(OUTPUT[8]), .sel(in_6));  // open: en
  Multiplexer multiplexer_53 (
    .in0(multiplexer_51_out), .in1(multiplexer_50_out), .out(OUTPUT[9]), .sel(in_6));  // open: en
  Multiplexer multiplexer_54 (.in0(Input[11]), .in1(1'b0), .out(multiplexer_54_out), .sel(in_2));  // open: en
  Multiplexer multiplexer_55 (.in0(Input[12]), .in1(1'b0), .out(multiplexer_55_out), .sel(in_2));  // open: en
  Multiplexer multiplexer_56 (
    .in0(multiplexer_54_out), .in1(multiplexer_15_out), .out(multiplexer_56_out), .sel(in_3));  // open: en
  Multiplexer multiplexer_57 (
    .in0(multiplexer_55_out), .in1(multiplexer_14_out), .out(multiplexer_57_out), .sel(in_3));  // open: en
  Multiplexer multiplexer_58 (
    .in0(multiplexer_57_out), .in1(multiplexer_36_out), .out(multiplexer_58_out), .sel(in_4));  // open: en
  Multiplexer multiplexer_59 (
    .in0(multiplexer_56_out), .in1(multiplexer_37_out), .out(multiplexer_59_out), .sel(in_4));  // open: en
  Multiplexer multiplexer_60 (
    .in0(multiplexer_59_out), .in1(multiplexer_48_out), .out(multiplexer_60_out), .sel(in_5));  // open: en
  Multiplexer multiplexer_61 (
    .in0(multiplexer_49_out), .in1(multiplexer_38_out), .out(multiplexer_61_out), .sel(in_5));  // open: en
  Multiplexer multiplexer_62 (
    .in0(multiplexer_61_out), .in1(multiplexer_51_out), .out(OUTPUT[10]), .sel(in_6));  // open: en
  Multiplexer multiplexer_63 (
    .in0(multiplexer_60_out), .in1(multiplexer_61_out), .out(OUTPUT[11]), .sel(in_6));  // open: en
  Multiplexer multiplexer_64 (.in0(Input[14]), .in1(1'b0), .out(multiplexer_64_out), .sel(in_2));  // open: en
  Multiplexer multiplexer_65 (.in0(Input[13]), .in1(1'b0), .out(multiplexer_65_out), .sel(in_2));  // open: en
  Multiplexer multiplexer_66 (
    .in0(multiplexer_65_out), .in1(multiplexer_24_out), .out(multiplexer_66_out), .sel(in_3));  // open: en
  Multiplexer multiplexer_67 (
    .in0(multiplexer_64_out), .in1(multiplexer_25_out), .out(multiplexer_67_out), .sel(in_3));  // open: en
  Multiplexer multiplexer_68 (
    .in0(multiplexer_66_out), .in1(multiplexer_47_out), .out(multiplexer_68_out), .sel(in_4));  // open: en
  Multiplexer multiplexer_69 (
    .in0(multiplexer_67_out), .in1(multiplexer_46_out), .out(multiplexer_69_out), .sel(in_4));  // open: en
  Multiplexer multiplexer_70 (
    .in0(multiplexer_58_out), .in1(multiplexer_49_out), .out(multiplexer_70_out), .sel(in_5));  // open: en
  Multiplexer multiplexer_71 (
    .in0(multiplexer_68_out), .in1(multiplexer_59_out), .out(multiplexer_71_out), .sel(in_5));  // open: en
  Multiplexer multiplexer_72 (
    .in0(multiplexer_71_out), .in1(multiplexer_70_out), .out(OUTPUT[13]), .sel(in_6));  // open: en
  Multiplexer multiplexer_73 (
    .in0(multiplexer_70_out), .in1(multiplexer_60_out), .out(OUTPUT[12]), .sel(in_6));  // open: en
  Multiplexer multiplexer_74 (.in0(Input[15]), .in1(1'b0), .out(multiplexer_74_out), .sel(in_2));  // open: en
  Multiplexer multiplexer_75 (.in0(Input[16]), .in1(Input[0]), .out(multiplexer_75_out), .sel(in_2));  // open: en
  Multiplexer multiplexer_76 (
    .in0(multiplexer_75_out), .in1(multiplexer_34_out), .out(multiplexer_76_out), .sel(in_3));  // open: en
  Multiplexer multiplexer_77 (
    .in0(multiplexer_74_out), .in1(multiplexer_35_out), .out(multiplexer_77_out), .sel(in_3));  // open: en
  Multiplexer multiplexer_78 (
    .in0(multiplexer_76_out), .in1(multiplexer_57_out), .out(multiplexer_78_out), .sel(in_4));  // open: en
  Multiplexer multiplexer_79 (
    .in0(multiplexer_77_out), .in1(multiplexer_56_out), .out(multiplexer_79_out), .sel(in_4));  // open: en
  Multiplexer multiplexer_80 (
    .in0(multiplexer_69_out), .in1(multiplexer_58_out), .out(multiplexer_80_out), .sel(in_5));  // open: en
  Multiplexer multiplexer_81 (
    .in0(multiplexer_79_out), .in1(multiplexer_68_out), .out(multiplexer_81_out), .sel(in_5));  // open: en
  Multiplexer multiplexer_82 (
    .in0(multiplexer_81_out), .in1(multiplexer_80_out), .out(OUTPUT[15]), .sel(in_6));  // open: en
  Multiplexer multiplexer_83 (
    .in0(multiplexer_80_out), .in1(multiplexer_71_out), .out(OUTPUT[14]), .sel(in_6));  // open: en
  Multiplexer multiplexer_84 (.in0(Input[17]), .in1(Input[1]), .out(multiplexer_84_out), .sel(in_2));  // open: en
  Multiplexer multiplexer_85 (.in0(Input[18]), .in1(Input[2]), .out(multiplexer_85_out), .sel(in_2));  // open: en
  Multiplexer multiplexer_86 (
    .in0(multiplexer_84_out), .in1(multiplexer_44_out), .out(multiplexer_86_out), .sel(in_3));  // open: en
  Multiplexer multiplexer_87 (
    .in0(multiplexer_85_out), .in1(multiplexer_45_out), .out(multiplexer_87_out), .sel(in_3));  // open: en
  Multiplexer multiplexer_88 (
    .in0(multiplexer_87_out), .in1(multiplexer_67_out), .out(multiplexer_88_out), .sel(in_4));  // open: en
  Multiplexer multiplexer_89 (
    .in0(multiplexer_86_out), .in1(multiplexer_66_out), .out(multiplexer_89_out), .sel(in_4));  // open: en
  Multiplexer multiplexer_90 (
    .in0(multiplexer_89_out), .in1(multiplexer_79_out), .out(multiplexer_90_out), .sel(in_5));  // open: en
  Multiplexer multiplexer_91 (
    .in0(multiplexer_78_out), .in1(multiplexer_69_out), .out(multiplexer_91_out), .sel(in_5));  // open: en
  Multiplexer multiplexer_92 (
    .in0(multiplexer_91_out), .in1(multiplexer_81_out), .out(OUTPUT[16]), .sel(in_6));  // open: en
  Multiplexer multiplexer_93 (
    .in0(multiplexer_90_out), .in1(multiplexer_91_out), .out(OUTPUT[17]), .sel(in_6));  // open: en
  Multiplexer multiplexer_94 (.in0(Input[19]), .in1(Input[3]), .out(multiplexer_94_out), .sel(in_2));  // open: en
  Multiplexer multiplexer_95 (.in0(Input[20]), .in1(Input[4]), .out(multiplexer_95_out), .sel(in_2));  // open: en
  Multiplexer multiplexer_96 (
    .in0(multiplexer_94_out), .in1(multiplexer_54_out), .out(multiplexer_96_out), .sel(in_3));  // open: en
  Multiplexer multiplexer_97 (
    .in0(multiplexer_95_out), .in1(multiplexer_55_out), .out(multiplexer_97_out), .sel(in_3));  // open: en
  Multiplexer multiplexer_98 (
    .in0(multiplexer_97_out), .in1(multiplexer_76_out), .out(multiplexer_98_out), .sel(in_4));  // open: en
  Multiplexer multiplexer_99 (
    .in0(multiplexer_96_out), .in1(multiplexer_77_out), .out(multiplexer_99_out), .sel(in_4));  // open: en
  Multiplexer multiplexer_100 (
    .in0(multiplexer_88_out), .in1(multiplexer_78_out), .out(multiplexer_100_out), .sel(in_5));  // open: en
  Multiplexer multiplexer_101 (
    .in0(multiplexer_99_out), .in1(multiplexer_89_out), .out(multiplexer_101_out), .sel(in_5));  // open: en
  Multiplexer multiplexer_102 (
    .in0(multiplexer_100_out), .in1(multiplexer_90_out), .out(OUTPUT[18]), .sel(in_6));  // open: en
  Multiplexer multiplexer_103 (
    .in0(multiplexer_101_out), .in1(multiplexer_100_out), .out(OUTPUT[19]), .sel(in_6));  // open: en
  Multiplexer multiplexer_104 (.in0(Input[21]), .in1(Input[5]), .out(multiplexer_104_out), .sel(in_2));  // open: en
  Multiplexer multiplexer_105 (.in0(Input[22]), .in1(Input[6]), .out(multiplexer_105_out), .sel(in_2));  // open: en
  Multiplexer multiplexer_106 (
    .in0(multiplexer_104_out), .in1(multiplexer_65_out), .out(multiplexer_106_out), .sel(in_3));  // open: en
  Multiplexer multiplexer_107 (
    .in0(multiplexer_105_out), .in1(multiplexer_64_out), .out(multiplexer_107_out), .sel(in_3));  // open: en
  Multiplexer multiplexer_108 (
    .in0(multiplexer_107_out), .in1(multiplexer_87_out), .out(multiplexer_108_out), .sel(in_4));  // open: en
  Multiplexer multiplexer_109 (
    .in0(multiplexer_106_out), .in1(multiplexer_86_out), .out(multiplexer_109_out), .sel(in_4));  // open: en
  Multiplexer multiplexer_110 (
    .in0(multiplexer_98_out), .in1(multiplexer_88_out), .out(multiplexer_110_out), .sel(in_5));  // open: en
  Multiplexer multiplexer_111 (
    .in0(multiplexer_109_out), .in1(multiplexer_99_out), .out(multiplexer_111_out), .sel(in_5));  // open: en
  Multiplexer multiplexer_112 (
    .in0(multiplexer_110_out), .in1(multiplexer_101_out), .out(OUTPUT[20]), .sel(in_6));  // open: en
  Multiplexer multiplexer_113 (
    .in0(multiplexer_111_out), .in1(multiplexer_110_out), .out(OUTPUT[21]), .sel(in_6));  // open: en
  Multiplexer multiplexer_114 (.in0(Input[23]), .in1(Input[7]), .out(multiplexer_114_out), .sel(in_2));  // open: en
  Multiplexer multiplexer_115 (.in0(Input[24]), .in1(Input[8]), .out(multiplexer_115_out), .sel(in_2));  // open: en
  Multiplexer multiplexer_116 (
    .in0(multiplexer_115_out), .in1(multiplexer_75_out), .out(multiplexer_116_out), .sel(in_3));  // open: en
  Multiplexer multiplexer_117 (
    .in0(multiplexer_114_out), .in1(multiplexer_74_out), .out(multiplexer_117_out), .sel(in_3));  // open: en
  Multiplexer multiplexer_118 (
    .in0(multiplexer_116_out), .in1(multiplexer_97_out), .out(multiplexer_118_out), .sel(in_4));  // open: en
  Multiplexer multiplexer_119 (
    .in0(multiplexer_117_out), .in1(multiplexer_96_out), .out(multiplexer_119_out), .sel(in_4));  // open: en
  Multiplexer multiplexer_120 (
    .in0(multiplexer_108_out), .in1(multiplexer_98_out), .out(multiplexer_120_out), .sel(in_5));  // open: en
  Multiplexer multiplexer_121 (
    .in0(multiplexer_119_out), .in1(multiplexer_109_out), .out(multiplexer_121_out), .sel(in_5));  // open: en
  Multiplexer multiplexer_122 (
    .in0(multiplexer_120_out), .in1(multiplexer_111_out), .out(OUTPUT[22]), .sel(in_6));  // open: en
  Multiplexer multiplexer_123 (
    .in0(multiplexer_121_out), .in1(multiplexer_120_out), .out(OUTPUT[23]), .sel(in_6));  // open: en
  Multiplexer multiplexer_124 (.in0(Input[25]), .in1(Input[9]), .out(multiplexer_124_out), .sel(in_2));  // open: en
  Multiplexer multiplexer_125 (.in0(Input[26]), .in1(Input[10]), .out(multiplexer_125_out), .sel(in_2));  // open: en
  Multiplexer multiplexer_126 (
    .in0(multiplexer_125_out), .in1(multiplexer_85_out), .out(multiplexer_126_out), .sel(in_3));  // open: en
  Multiplexer multiplexer_127 (
    .in0(multiplexer_124_out), .in1(multiplexer_84_out), .out(multiplexer_127_out), .sel(in_3));  // open: en
  Multiplexer multiplexer_128 (
    .in0(multiplexer_126_out), .in1(multiplexer_107_out), .out(multiplexer_128_out), .sel(in_4));  // open: en
  Multiplexer multiplexer_129 (
    .in0(multiplexer_127_out), .in1(multiplexer_106_out), .out(multiplexer_129_out), .sel(in_4));  // open: en
  Multiplexer multiplexer_130 (
    .in0(multiplexer_118_out), .in1(multiplexer_108_out), .out(multiplexer_130_out), .sel(in_5));  // open: en
  Multiplexer multiplexer_131 (
    .in0(multiplexer_129_out), .in1(multiplexer_119_out), .out(multiplexer_131_out), .sel(in_5));  // open: en
  Multiplexer multiplexer_132 (
    .in0(multiplexer_131_out), .in1(multiplexer_130_out), .out(OUTPUT[25]), .sel(in_6));  // open: en
  Multiplexer multiplexer_133 (
    .in0(multiplexer_130_out), .in1(multiplexer_121_out), .out(OUTPUT[24]), .sel(in_6));  // open: en
  Multiplexer multiplexer_134 (.in0(Input[27]), .in1(Input[11]), .out(multiplexer_134_out), .sel(in_2));  // open: en
  Multiplexer multiplexer_135 (.in0(Input[28]), .in1(Input[12]), .out(multiplexer_135_out), .sel(in_2));  // open: en
  Multiplexer multiplexer_136 (
    .in0(multiplexer_134_out), .in1(multiplexer_94_out), .out(multiplexer_136_out), .sel(in_3));  // open: en
  Multiplexer multiplexer_137 (
    .in0(multiplexer_135_out), .in1(multiplexer_95_out), .out(multiplexer_137_out), .sel(in_3));  // open: en
  Multiplexer multiplexer_138 (
    .in0(multiplexer_136_out), .in1(multiplexer_117_out), .out(multiplexer_138_out), .sel(in_4));  // open: en
  Multiplexer multiplexer_139 (
    .in0(multiplexer_137_out), .in1(multiplexer_116_out), .out(multiplexer_139_out), .sel(in_4));  // open: en
  Multiplexer multiplexer_140 (
    .in0(multiplexer_128_out), .in1(multiplexer_118_out), .out(multiplexer_140_out), .sel(in_5));  // open: en
  Multiplexer multiplexer_141 (
    .in0(multiplexer_138_out), .in1(multiplexer_129_out), .out(multiplexer_141_out), .sel(in_5));  // open: en
  Multiplexer multiplexer_142 (
    .in0(multiplexer_140_out), .in1(multiplexer_131_out), .out(OUTPUT[26]), .sel(in_6));  // open: en
  Multiplexer multiplexer_143 (
    .in0(multiplexer_141_out), .in1(multiplexer_140_out), .out(OUTPUT[27]), .sel(in_6));  // open: en
  Multiplexer multiplexer_144 (.in0(Input[29]), .in1(Input[13]), .out(multiplexer_144_out), .sel(in_2));  // open: en
  Multiplexer multiplexer_145 (.in0(Input[30]), .in1(Input[14]), .out(multiplexer_145_out), .sel(in_2));  // open: en
  Multiplexer multiplexer_146 (
    .in0(multiplexer_145_out), .in1(multiplexer_105_out), .out(multiplexer_146_out), .sel(in_3));  // open: en
  Multiplexer multiplexer_147 (
    .in0(multiplexer_144_out), .in1(multiplexer_104_out), .out(multiplexer_147_out), .sel(in_3));  // open: en
  Multiplexer multiplexer_148 (
    .in0(multiplexer_147_out), .in1(multiplexer_127_out), .out(multiplexer_148_out), .sel(in_4));  // open: en
  Multiplexer multiplexer_149 (
    .in0(multiplexer_146_out), .in1(multiplexer_126_out), .out(multiplexer_149_out), .sel(in_4));  // open: en
  Multiplexer multiplexer_150 (
    .in0(multiplexer_139_out), .in1(multiplexer_128_out), .out(multiplexer_150_out), .sel(in_5));  // open: en
  Multiplexer multiplexer_151 (
    .in0(multiplexer_148_out), .in1(multiplexer_138_out), .out(multiplexer_151_out), .sel(in_5));  // open: en
  Multiplexer multiplexer_152 (
    .in0(multiplexer_150_out), .in1(multiplexer_141_out), .out(OUTPUT[28]), .sel(in_6));  // open: en
  Multiplexer multiplexer_153 (
    .in0(multiplexer_151_out), .in1(multiplexer_150_out), .out(OUTPUT[29]), .sel(in_6));  // open: en
  Multiplexer multiplexer_154 (.in0(Input[31]), .in1(Input[15]), .out(multiplexer_154_out), .sel(in_2));  // open: en
  Multiplexer multiplexer_155 (
    .in0(multiplexer_154_out), .in1(multiplexer_114_out), .out(multiplexer_155_out), .sel(in_3));  // open: en
  Multiplexer multiplexer_156 (
    .in0(multiplexer_155_out), .in1(multiplexer_136_out), .out(multiplexer_156_out), .sel(in_4));  // open: en
  Multiplexer multiplexer_157 (
    .in0(multiplexer_156_out), .in1(multiplexer_148_out), .out(multiplexer_157_out), .sel(in_5));  // open: en
  Multiplexer multiplexer_158 (
    .in0(multiplexer_149_out), .in1(multiplexer_139_out), .out(multiplexer_158_out), .sel(in_5));  // open: en
  Multiplexer multiplexer_159 (
    .in0(multiplexer_157_out), .in1(multiplexer_158_out), .out(OUTPUT[31]), .sel(in_6));  // open: en
  Multiplexer multiplexer_160 (
    .in0(multiplexer_158_out), .in1(multiplexer_151_out), .out(OUTPUT[30]), .sel(in_6));  // open: en
endmodule

module _32b_Adder (
  input  [31:0] A,
  input  [31:0] B,
  output [31:0] Result,
  output out_4
);

  wire full_adder_1_carry_out, full_adder_2_carry_out, full_adder_3_carry_out, full_adder_4_carry_out,
       full_adder_5_carry_out, full_adder_6_carry_out, full_adder_7_carry_out, full_adder_8_carry_out,
       full_adder_9_carry_out, full_adder_10_carry_out, full_adder_11_carry_out, full_adder_12_carry_out,
       full_adder_13_carry_out, full_adder_14_carry_out, full_adder_15_carry_out, full_adder_16_carry_out,
       full_adder_17_carry_out, full_adder_18_carry_out, full_adder_19_carry_out, full_adder_20_carry_out,
       full_adder_21_carry_out, full_adder_22_carry_out, full_adder_23_carry_out, full_adder_24_carry_out,
       full_adder_25_carry_out, full_adder_26_carry_out, full_adder_27_carry_out, full_adder_28_carry_out,
       full_adder_29_carry_out, full_adder_30_carry_out, full_adder_31_carry_out;

  Full_Adder full_adder_1 (
    .A(A[24]), .B(B[24]), .Carry_In(1'b0), .Result(Result[24]), .Carry_out(full_adder_1_carry_out));
  Full_Adder full_adder_2 (
    .A(A[25]), .B(B[25]), .Carry_In(full_adder_1_carry_out), .Result(Result[25]),
    .Carry_out(full_adder_2_carry_out));
  Full_Adder full_adder_3 (
    .A(A[26]), .B(B[26]), .Carry_In(full_adder_2_carry_out), .Result(Result[26]),
    .Carry_out(full_adder_3_carry_out));
  Full_Adder full_adder_4 (
    .A(A[27]), .B(B[27]), .Carry_In(full_adder_3_carry_out), .Result(Result[27]),
    .Carry_out(full_adder_4_carry_out));
  Full_Adder full_adder_5 (
    .A(A[28]), .B(B[28]), .Carry_In(full_adder_4_carry_out), .Result(Result[28]),
    .Carry_out(full_adder_5_carry_out));
  Full_Adder full_adder_6 (
    .A(A[29]), .B(B[29]), .Carry_In(full_adder_5_carry_out), .Result(Result[29]),
    .Carry_out(full_adder_6_carry_out));
  Full_Adder full_adder_7 (
    .A(A[30]), .B(B[30]), .Carry_In(full_adder_6_carry_out), .Result(Result[30]),
    .Carry_out(full_adder_7_carry_out));
  Full_Adder full_adder_8 (
    .A(A[31]), .B(B[31]), .Carry_In(full_adder_7_carry_out), .Result(Result[31]),
    .Carry_out(full_adder_8_carry_out));
  Full_Adder full_adder_9 (
    .A(A[16]), .B(B[16]), .Carry_In(full_adder_8_carry_out), .Result(Result[16]),
    .Carry_out(full_adder_9_carry_out));
  Full_Adder full_adder_10 (
    .A(A[17]), .B(B[17]), .Carry_In(full_adder_9_carry_out), .Result(Result[17]),
    .Carry_out(full_adder_10_carry_out));
  Full_Adder full_adder_11 (
    .A(A[18]), .B(B[18]), .Carry_In(full_adder_10_carry_out), .Result(Result[18]),
    .Carry_out(full_adder_11_carry_out));
  Full_Adder full_adder_12 (
    .A(A[19]), .B(B[19]), .Carry_In(full_adder_11_carry_out), .Result(Result[19]),
    .Carry_out(full_adder_12_carry_out));
  Full_Adder full_adder_13 (
    .A(A[20]), .B(B[20]), .Carry_In(full_adder_12_carry_out), .Result(Result[20]),
    .Carry_out(full_adder_13_carry_out));
  Full_Adder full_adder_14 (
    .A(A[21]), .B(B[21]), .Carry_In(full_adder_13_carry_out), .Result(Result[21]),
    .Carry_out(full_adder_14_carry_out));
  Full_Adder full_adder_15 (
    .A(A[22]), .B(B[22]), .Carry_In(full_adder_14_carry_out), .Result(Result[22]),
    .Carry_out(full_adder_15_carry_out));
  Full_Adder full_adder_16 (
    .A(A[23]), .B(B[23]), .Carry_In(full_adder_15_carry_out), .Result(Result[23]),
    .Carry_out(full_adder_16_carry_out));
  Full_Adder full_adder_17 (
    .A(A[8]), .B(B[8]), .Carry_In(full_adder_16_carry_out), .Result(Result[8]),
    .Carry_out(full_adder_17_carry_out));
  Full_Adder full_adder_18 (
    .A(A[9]), .B(B[9]), .Carry_In(full_adder_17_carry_out), .Result(Result[9]),
    .Carry_out(full_adder_18_carry_out));
  Full_Adder full_adder_19 (
    .A(A[10]), .B(B[10]), .Carry_In(full_adder_18_carry_out), .Result(Result[10]),
    .Carry_out(full_adder_19_carry_out));
  Full_Adder full_adder_20 (
    .A(A[11]), .B(B[11]), .Carry_In(full_adder_19_carry_out), .Result(Result[11]),
    .Carry_out(full_adder_20_carry_out));
  Full_Adder full_adder_21 (
    .A(A[12]), .B(B[12]), .Carry_In(full_adder_20_carry_out), .Result(Result[12]),
    .Carry_out(full_adder_21_carry_out));
  Full_Adder full_adder_22 (
    .A(A[13]), .B(B[13]), .Carry_In(full_adder_21_carry_out), .Result(Result[13]),
    .Carry_out(full_adder_22_carry_out));
  Full_Adder full_adder_23 (
    .A(A[14]), .B(B[14]), .Carry_In(full_adder_22_carry_out), .Result(Result[14]),
    .Carry_out(full_adder_23_carry_out));
  Full_Adder full_adder_24 (
    .A(A[15]), .B(B[15]), .Carry_In(full_adder_23_carry_out), .Result(Result[15]),
    .Carry_out(full_adder_24_carry_out));
  Full_Adder full_adder_25 (
    .A(A[0]), .B(B[0]), .Carry_In(full_adder_24_carry_out), .Result(Result[0]),
    .Carry_out(full_adder_25_carry_out));
  Full_Adder full_adder_26 (
    .A(A[1]), .B(B[1]), .Carry_In(full_adder_25_carry_out), .Result(Result[1]),
    .Carry_out(full_adder_26_carry_out));
  Full_Adder full_adder_27 (
    .A(A[2]), .B(B[2]), .Carry_In(full_adder_26_carry_out), .Result(Result[2]),
    .Carry_out(full_adder_27_carry_out));
  Full_Adder full_adder_28 (
    .A(A[3]), .B(B[3]), .Carry_In(full_adder_27_carry_out), .Result(Result[3]),
    .Carry_out(full_adder_28_carry_out));
  Full_Adder full_adder_29 (
    .A(A[4]), .B(B[4]), .Carry_In(full_adder_28_carry_out), .Result(Result[4]),
    .Carry_out(full_adder_29_carry_out));
  Full_Adder full_adder_30 (
    .A(A[5]), .B(B[5]), .Carry_In(full_adder_29_carry_out), .Result(Result[5]),
    .Carry_out(full_adder_30_carry_out));
  Full_Adder full_adder_31 (
    .A(A[6]), .B(B[6]), .Carry_In(full_adder_30_carry_out), .Result(Result[6]),
    .Carry_out(full_adder_31_carry_out));
  Full_Adder full_adder_32 (
    .A(A[7]), .B(B[7]), .Carry_In(full_adder_31_carry_out), .Result(Result[7]), .Carry_out(out_4));
endmodule

module _32b_Subtract (
  input  Carry_In,
  input  [31:0] A,
  input  [31:0] B,
  output [31:0] out_4,
  output Carry_Out
);

  wire n4_bit_cla_1_c4, n4_bit_cla_2_c4, n4_bit_cla_3_c4, n4_bit_cla_4_c4, n4_bit_cla_5_c4, n4_bit_cla_6_c4,
       n4_bit_cla_7_c4;
  wire [31:0] n2_s_complement_1_out_2;

  _2_s_Complement u_2_s_complement_1 (.A(B), .out_2(n2_s_complement_1_out_2));
  _4_bit_CLA u_4_bit_cla_1 (
    .C0(Carry_In), .A0(A[0]), .A0_2(A[1]), .A0_3(A[2]), .A0_4(A[3]), .B0(n2_s_complement_1_out_2[0]),
    .B0_2(n2_s_complement_1_out_2[1]), .B0_3(n2_s_complement_1_out_2[2]), .B0_4(n2_s_complement_1_out_2[3]),
    .S0(out_4[0]), .S1(out_4[1]), .S2(out_4[2]), .S3(out_4[3]), .C4(n4_bit_cla_1_c4));
  _4_bit_CLA u_4_bit_cla_2 (
    .C0(n4_bit_cla_1_c4), .A0(A[4]), .A0_2(A[5]), .A0_3(A[6]), .A0_4(A[7]), .B0(n2_s_complement_1_out_2[4]),
    .B0_2(n2_s_complement_1_out_2[5]), .B0_3(n2_s_complement_1_out_2[6]), .B0_4(n2_s_complement_1_out_2[7]),
    .S0(out_4[4]), .S1(out_4[5]), .S2(out_4[6]), .S3(out_4[7]), .C4(n4_bit_cla_2_c4));
  _4_bit_CLA u_4_bit_cla_3 (
    .C0(n4_bit_cla_2_c4), .A0(A[8]), .A0_2(A[9]), .A0_3(A[10]), .A0_4(A[11]),
    .B0(n2_s_complement_1_out_2[8]), .B0_2(n2_s_complement_1_out_2[9]), .B0_3(n2_s_complement_1_out_2[10]),
    .B0_4(n2_s_complement_1_out_2[11]), .S0(out_4[8]), .S1(out_4[9]), .S2(out_4[10]), .S3(out_4[11]),
    .C4(n4_bit_cla_3_c4));
  _4_bit_CLA u_4_bit_cla_4 (
    .C0(n4_bit_cla_3_c4), .A0(A[12]), .A0_2(A[13]), .A0_3(A[14]), .A0_4(A[15]),
    .B0(n2_s_complement_1_out_2[12]), .B0_2(n2_s_complement_1_out_2[13]), .B0_3(n2_s_complement_1_out_2[14]),
    .B0_4(n2_s_complement_1_out_2[15]), .S0(out_4[12]), .S1(out_4[13]), .S2(out_4[14]), .S3(out_4[15]),
    .C4(n4_bit_cla_4_c4));
  _4_bit_CLA u_4_bit_cla_5 (
    .C0(n4_bit_cla_4_c4), .A0(A[16]), .A0_2(A[17]), .A0_3(A[18]), .A0_4(A[19]),
    .B0(n2_s_complement_1_out_2[16]), .B0_2(n2_s_complement_1_out_2[17]), .B0_3(n2_s_complement_1_out_2[18]),
    .B0_4(n2_s_complement_1_out_2[19]), .S0(out_4[16]), .S1(out_4[17]), .S2(out_4[18]), .S3(out_4[19]),
    .C4(n4_bit_cla_5_c4));
  _4_bit_CLA u_4_bit_cla_6 (
    .C0(n4_bit_cla_5_c4), .A0(A[20]), .A0_2(A[21]), .A0_3(A[22]), .A0_4(A[23]),
    .B0(n2_s_complement_1_out_2[20]), .B0_2(n2_s_complement_1_out_2[21]), .B0_3(n2_s_complement_1_out_2[22]),
    .B0_4(n2_s_complement_1_out_2[23]), .S0(out_4[20]), .S1(out_4[21]), .S2(out_4[22]), .S3(out_4[23]),
    .C4(n4_bit_cla_6_c4));
  _4_bit_CLA u_4_bit_cla_7 (
    .C0(n4_bit_cla_6_c4), .A0(A[24]), .A0_2(A[25]), .A0_3(A[26]), .A0_4(A[27]),
    .B0(n2_s_complement_1_out_2[24]), .B0_2(n2_s_complement_1_out_2[25]), .B0_3(n2_s_complement_1_out_2[26]),
    .B0_4(n2_s_complement_1_out_2[27]), .S0(out_4[24]), .S1(out_4[25]), .S2(out_4[26]), .S3(out_4[27]),
    .C4(n4_bit_cla_7_c4));
  _4_bit_CLA u_4_bit_cla_8 (
    .C0(n4_bit_cla_7_c4), .A0(A[28]), .A0_2(A[29]), .A0_3(A[30]), .A0_4(A[31]),
    .B0(n2_s_complement_1_out_2[28]), .B0_2(n2_s_complement_1_out_2[29]), .B0_3(n2_s_complement_1_out_2[30]),
    .B0_4(n2_s_complement_1_out_2[31]), .S0(out_4[28]), .S1(out_4[29]), .S2(out_4[30]), .S3(out_4[31]),
    .C4(Carry_Out));
endmodule

module _4_bit_CLA (
  input  C0,
  input  A0,
  input  A0_2,
  input  A0_3,
  input  A0_4,
  input  B0,
  input  B0_2,
  input  B0_3,
  input  B0_4,
  output S0,
  output S1,
  output S2,
  output S3,
  output C4
);

  wire and_1_out, and_2_out, and_3_out, and_4_out, and_5_out, and_6_out, and_7_out, and_8_out, and_9_out,
       and_10_out, and_11_out, and_12_out, and_13_out, and_14_out, or_1_out, or_2_out, or_3_out, xor_1_out,
       xor_2_out, xor_3_out, xor_4_out;

  xor xor_1 (xor_1_out, B0, A0);
  and and_1 (and_1_out, A0, B0);
  or or_1 (or_1_out, and_1_out, and_5_out);
  xor xor_2 (xor_2_out, B0_2, A0_2);
  and and_2 (and_2_out, A0_2, B0_2);
  or or_2 (or_2_out, and_2_out, and_6_out, and_7_out);
  xor xor_3 (xor_3_out, B0_3, A0_3);
  and and_3 (and_3_out, A0_3, B0_3);
  or or_3 (or_3_out, and_3_out, and_8_out, and_9_out, and_10_out);
  xor xor_4 (xor_4_out, B0_4, A0_4);
  and and_4 (and_4_out, A0_4, B0_4);
  or or_4 (C4, and_4_out, and_11_out, and_12_out, and_13_out, and_14_out);
  xor xor_5 (S0, C0, xor_1_out);
  xor xor_6 (S1, or_1_out, xor_2_out);
  xor xor_7 (S2, or_2_out, xor_3_out);
  xor xor_8 (S3, or_3_out, xor_4_out);
  and and_5 (and_5_out, xor_1_out, C0);
  and and_6 (and_6_out, xor_2_out, and_1_out);
  and and_7 (and_7_out, xor_2_out, xor_1_out, C0);
  and and_8 (and_8_out, xor_3_out, and_2_out);
  and and_9 (and_9_out, xor_3_out, xor_2_out, and_1_out);
  and and_10 (and_10_out, xor_3_out, xor_2_out, xor_1_out, C0);
  and and_11 (and_11_out, xor_4_out, and_3_out);
  and and_12 (and_12_out, xor_4_out, xor_3_out, and_2_out);
  and and_13 (and_13_out, xor_4_out, xor_3_out, xor_2_out, and_1_out);
  and and_14 (and_14_out, xor_4_out, xor_3_out, xor_2_out, xor_1_out, C0);
endmodule

module CLA__Carry_lookahead_adder (
  input  Carry_In,
  input  [31:0] A,
  input  [31:0] B,
  output [31:0] out_4,
  output Carry_Out
);

  wire n4_bit_cla_1_c4, n4_bit_cla_2_c4, n4_bit_cla_3_c4, n4_bit_cla_4_c4, n4_bit_cla_5_c4, n4_bit_cla_6_c4,
       n4_bit_cla_7_c4;

  _4_bit_CLA u_4_bit_cla_1 (
    .C0(Carry_In), .A0(A[0]), .A0_2(A[1]), .A0_3(A[2]), .A0_4(A[3]), .B0(B[0]), .B0_2(B[1]), .B0_3(B[2]),
    .B0_4(B[3]), .S0(out_4[0]), .S1(out_4[1]), .S2(out_4[2]), .S3(out_4[3]), .C4(n4_bit_cla_1_c4));
  _4_bit_CLA u_4_bit_cla_2 (
    .C0(n4_bit_cla_1_c4), .A0(A[4]), .A0_2(A[5]), .A0_3(A[6]), .A0_4(A[7]), .B0(B[4]), .B0_2(B[5]),
    .B0_3(B[6]), .B0_4(B[7]), .S0(out_4[4]), .S1(out_4[5]), .S2(out_4[6]), .S3(out_4[7]), .C4(n4_bit_cla_2_c4));
  _4_bit_CLA u_4_bit_cla_3 (
    .C0(n4_bit_cla_2_c4), .A0(A[8]), .A0_2(A[9]), .A0_3(A[10]), .A0_4(A[11]), .B0(B[8]), .B0_2(B[9]),
    .B0_3(B[10]), .B0_4(B[11]), .S0(out_4[8]), .S1(out_4[9]), .S2(out_4[10]), .S3(out_4[11]),
    .C4(n4_bit_cla_3_c4));
  _4_bit_CLA u_4_bit_cla_4 (
    .C0(n4_bit_cla_3_c4), .A0(A[12]), .A0_2(A[13]), .A0_3(A[14]), .A0_4(A[15]), .B0(B[12]), .B0_2(B[13]),
    .B0_3(B[14]), .B0_4(B[15]), .S0(out_4[12]), .S1(out_4[13]), .S2(out_4[14]), .S3(out_4[15]),
    .C4(n4_bit_cla_4_c4));
  _4_bit_CLA u_4_bit_cla_5 (
    .C0(n4_bit_cla_4_c4), .A0(A[16]), .A0_2(A[17]), .A0_3(A[18]), .A0_4(A[19]), .B0(B[16]), .B0_2(B[17]),
    .B0_3(B[18]), .B0_4(B[19]), .S0(out_4[16]), .S1(out_4[17]), .S2(out_4[18]), .S3(out_4[19]),
    .C4(n4_bit_cla_5_c4));
  _4_bit_CLA u_4_bit_cla_6 (
    .C0(n4_bit_cla_5_c4), .A0(A[20]), .A0_2(A[21]), .A0_3(A[22]), .A0_4(A[23]), .B0(B[20]), .B0_2(B[21]),
    .B0_3(B[22]), .B0_4(B[23]), .S0(out_4[20]), .S1(out_4[21]), .S2(out_4[22]), .S3(out_4[23]),
    .C4(n4_bit_cla_6_c4));
  _4_bit_CLA u_4_bit_cla_7 (
    .C0(n4_bit_cla_6_c4), .A0(A[24]), .A0_2(A[25]), .A0_3(A[26]), .A0_4(A[27]), .B0(B[24]), .B0_2(B[25]),
    .B0_3(B[26]), .B0_4(B[27]), .S0(out_4[24]), .S1(out_4[25]), .S2(out_4[26]), .S3(out_4[27]),
    .C4(n4_bit_cla_7_c4));
  _4_bit_CLA u_4_bit_cla_8 (
    .C0(n4_bit_cla_7_c4), .A0(A[28]), .A0_2(A[29]), .A0_3(A[30]), .A0_4(A[31]), .B0(B[28]), .B0_2(B[29]),
    .B0_3(B[30]), .B0_4(B[31]), .S0(out_4[28]), .S1(out_4[29]), .S2(out_4[30]), .S3(out_4[31]), .C4(Carry_Out));
endmodule

// Set Less Than
module SLT__Set_Less_Than (
  input  [31:0] B,
  input  [31:0] A,
  output [31:0] out_3
);

  wire and_1_out, and_2_out, and_3_out, and_4_out, and_5_out, and_6_out, and_7_out, and_8_out, and_9_out,
       and_10_out, and_11_out, and_12_out, and_13_out, and_14_out, and_15_out, and_16_out, and_17_out,
       and_18_out, and_19_out, and_20_out, and_21_out, and_22_out, and_23_out, and_24_out, and_25_out,
       and_26_out, and_27_out, and_28_out, and_29_out, and_30_out, and_31_out, and_32_out, and_33_out,
       and_34_out, and_35_out, and_36_out, and_37_out, and_38_out, and_39_out, and_40_out, and_41_out,
       and_42_out, and_43_out, and_44_out, and_45_out, and_46_out, and_47_out, and_48_out, and_49_out,
       and_50_out, and_51_out, and_52_out, and_53_out, and_54_out, and_55_out, and_56_out, and_57_out,
       and_58_out, and_59_out, and_60_out, and_61_out, and_62_out, and_63_out, and_64_out, and_65_out,
       and_66_out, and_67_out, and_68_out, and_69_out, and_70_out, and_71_out, and_72_out, and_73_out,
       and_74_out, and_75_out, and_76_out, and_77_out, and_78_out, and_79_out, and_80_out, and_81_out,
       and_82_out, and_83_out, and_84_out, and_85_out, and_86_out, and_87_out, and_88_out, and_89_out,
       and_90_out, and_91_out, and_92_out, and_93_out, not_1_out, not_2_out, not_3_out, not_4_out, not_5_out,
       not_6_out, not_7_out, not_8_out, not_9_out, not_10_out, not_11_out, not_12_out, not_13_out,
       not_14_out, not_15_out, not_16_out, not_17_out, not_18_out, not_19_out, not_20_out, not_21_out,
       not_22_out, not_23_out, not_24_out, not_25_out, not_26_out, not_27_out, not_28_out, not_29_out,
       not_30_out, not_31_out, not_32_out, or_1_out, or_2_out, or_3_out, or_4_out, or_6_out, or_7_out,
       xnor_1_out, xnor_2_out, xnor_3_out, xnor_4_out, xnor_5_out, xnor_6_out, xnor_7_out, xnor_8_out,
       xnor_9_out, xnor_10_out, xnor_11_out, xnor_12_out, xnor_13_out, xnor_14_out, xnor_15_out, xnor_16_out,
       xnor_17_out, xnor_18_out, xnor_19_out, xnor_20_out, xnor_21_out, xnor_22_out, xnor_23_out,
       xnor_24_out, xnor_25_out, xnor_26_out, xnor_27_out, xnor_28_out, xnor_29_out, xnor_30_out, xnor_31_out;

  not not_1 (not_1_out, A[31]);
  and and_1 (and_1_out, not_1_out, B[0]);
  xnor xnor_1 (xnor_1_out, A[31], B[0]);
  and and_2 (and_2_out, xnor_1_out, and_3_out);
  not not_2 (not_2_out, A[30]);
  xnor xnor_2 (xnor_2_out, A[30], B[1]);
  and and_3 (and_3_out, not_2_out, B[1]);
  or or_1 (or_1_out, and_1_out, and_2_out, and_6_out, and_8_out, and_12_out);
  not not_3 (not_3_out, A[29]);
  and and_4 (and_4_out, not_3_out, B[2]);
  and and_5 (and_5_out, xnor_2_out, xnor_1_out);
  and and_6 (and_6_out, and_5_out, and_4_out);
  not not_4 (not_4_out, A[28]);
  xnor xnor_3 (xnor_3_out, A[29], B[2]);
  and and_7 (and_7_out, and_5_out, xnor_3_out);
  and and_8 (and_8_out, and_7_out, and_10_out);
  and and_9 (and_9_out, and_7_out, xnor_4_out);
  xnor xnor_4 (xnor_4_out, A[28], B[3]);
  and and_10 (and_10_out, not_4_out, B[3]);
  and and_11 (and_11_out, and_9_out, xnor_5_out);
  and and_12 (and_12_out, and_9_out, and_13_out);
  not not_5 (not_5_out, A[27]);
  and and_13 (and_13_out, not_5_out, B[4]);
  and and_14 (and_14_out, and_11_out, xnor_6_out);
  and and_15 (and_15_out, and_11_out, and_17_out);
  and and_16 (and_16_out, and_14_out, and_22_out);
  not not_6 (not_6_out, A[26]);
  xnor xnor_5 (xnor_5_out, A[27], B[4]);
  and and_17 (and_17_out, not_6_out, B[5]);
  and and_18 (and_18_out, and_14_out, xnor_7_out);
  and and_19 (and_19_out, and_18_out, and_25_out);
  or or_2 (or_2_out, and_15_out, and_16_out, and_19_out, and_21_out, and_24_out);
  not not_7 (not_7_out, A[25]);
  xnor xnor_6 (xnor_6_out, A[26], B[5]);
  and and_20 (and_20_out, and_18_out, xnor_8_out);
  and and_21 (and_21_out, and_20_out, and_28_out);
  xnor xnor_7 (xnor_7_out, A[25], B[6]);
  and and_22 (and_22_out, not_7_out, B[6]);
  and and_23 (and_23_out, and_20_out, xnor_9_out);
  and and_24 (and_24_out, and_23_out, and_34_out);
  not not_8 (not_8_out, A[24]);
  and and_25 (and_25_out, not_8_out, B[7]);
  and and_26 (and_26_out, and_23_out, xnor_10_out);
  and and_27 (and_27_out, and_26_out, and_38_out);
  not not_9 (not_9_out, A[23]);
  xnor xnor_8 (xnor_8_out, A[24], B[7]);
  and and_28 (and_28_out, not_9_out, B[8]);
  and and_29 (and_29_out, and_26_out, xnor_11_out);
  and and_30 (and_30_out, and_29_out, and_43_out);
  and and_31 (and_31_out, and_29_out, xnor_12_out);
  or or_3 (or_3_out, and_27_out, and_30_out, and_33_out, and_35_out, and_37_out);
  xnor xnor_9 (xnor_9_out, A[23], B[8]);
  and and_32 (and_32_out, and_31_out, xnor_13_out);
  and and_33 (and_33_out, and_31_out, and_46_out);
  not not_10 (not_10_out, A[22]);
  xnor xnor_10 (xnor_10_out, A[22], B[9]);
  and and_34 (and_34_out, not_10_out, B[9]);
  and and_35 (and_35_out, and_32_out, and_49_out);
  and and_36 (and_36_out, and_32_out, xnor_14_out);
  and and_37 (and_37_out, and_36_out, and_55_out);
  not not_11 (not_11_out, A[21]);
  and and_38 (and_38_out, not_11_out, B[10]);
  and and_39 (and_39_out, and_36_out, xnor_15_out);
  and and_40 (and_40_out, and_39_out, and_59_out);
  not not_12 (not_12_out, A[20]);
  xnor xnor_11 (xnor_11_out, A[21], B[10]);
  and and_41 (and_41_out, and_39_out, xnor_16_out);
  and and_42 (and_42_out, and_41_out, and_62_out);
  xnor xnor_12 (xnor_12_out, A[20], B[11]);
  and and_43 (and_43_out, not_12_out, B[11]);
  and and_44 (and_44_out, and_41_out, xnor_17_out);
  and and_45 (and_45_out, and_44_out, and_67_out);
  or or_4 (or_4_out, and_40_out, and_42_out, and_45_out, and_48_out, and_52_out);
  or or_5 (out_3[0], or_1_out, or_2_out, or_3_out, or_4_out, or_6_out, or_7_out, and_79_out, and_82_out);
  not not_13 (not_13_out, A[19]);
  and and_46 (and_46_out, not_13_out, B[12]);
  and and_47 (and_47_out, and_44_out, xnor_18_out);
  and and_48 (and_48_out, and_47_out, and_70_out);
  not not_14 (not_14_out, A[18]);
  xnor xnor_13 (xnor_13_out, A[19], B[12]);
  and and_49 (and_49_out, not_14_out, B[13]);
  and and_50 (and_50_out, and_47_out, xnor_19_out);
  and and_51 (and_51_out, and_50_out, xnor_20_out);
  and and_52 (and_52_out, and_50_out, and_76_out);
  not not_15 (not_15_out, A[17]);
  xnor xnor_14 (xnor_14_out, A[18], B[13]);
  and and_53 (and_53_out, and_51_out, and_80_out);
  and and_54 (and_54_out, and_51_out, xnor_21_out);
  xnor xnor_15 (xnor_15_out, A[17], B[14]);
  and and_55 (and_55_out, not_15_out, B[14]);
  and and_56 (and_56_out, and_54_out, and_83_out);
  and and_57 (and_57_out, and_54_out, xnor_22_out);
  and and_58 (and_58_out, and_57_out, and_84_out);
  or or_6 (or_6_out, and_53_out, and_56_out, and_58_out, and_61_out, and_64_out);
  not not_16 (not_16_out, A[16]);
  and and_59 (and_59_out, not_16_out, B[15]);
  and and_60 (and_60_out, and_57_out, xnor_23_out);
  and and_61 (and_61_out, and_60_out, and_85_out);
  not not_17 (not_17_out, A[15]);
  xnor xnor_16 (xnor_16_out, A[16], B[15]);
  and and_62 (and_62_out, not_17_out, B[16]);
  and and_63 (and_63_out, and_60_out, xnor_24_out);
  and and_64 (and_64_out, and_63_out, and_86_out);
  xnor xnor_17 (xnor_17_out, A[15], B[16]);
  and and_65 (and_65_out, and_63_out, xnor_25_out);
  and and_66 (and_66_out, and_65_out, and_87_out);
  not not_18 (not_18_out, A[14]);
  xnor xnor_18 (xnor_18_out, A[14], B[17]);
  and and_67 (and_67_out, not_18_out, B[17]);
  and and_68 (and_68_out, and_65_out, xnor_26_out);
  and and_69 (and_69_out, and_68_out, and_88_out);
  or or_7 (or_7_out, and_66_out, and_69_out, and_73_out, and_74_out, and_77_out);
  not not_19 (not_19_out, A[13]);
  and and_70 (and_70_out, not_19_out, B[18]);
  and and_71 (and_71_out, and_68_out, xnor_27_out);
  and and_72 (and_72_out, and_71_out, xnor_28_out);
  and and_73 (and_73_out, and_71_out, and_89_out);
  not not_20 (not_20_out, A[12]);
  xnor xnor_19 (xnor_19_out, A[13], B[18]);
  and and_74 (and_74_out, and_72_out, and_90_out);
  and and_75 (and_75_out, and_72_out, xnor_29_out);
  xnor xnor_20 (xnor_20_out, A[12], B[19]);
  and and_76 (and_76_out, not_20_out, B[19]);
  and and_77 (and_77_out, and_75_out, and_91_out);
  and and_78 (and_78_out, and_75_out, xnor_30_out);
  and and_79 (and_79_out, and_78_out, and_92_out);
  not not_21 (not_21_out, A[11]);
  and and_80 (and_80_out, not_21_out, B[20]);
  and and_81 (and_81_out, and_78_out, xnor_31_out);
  and and_82 (and_82_out, and_81_out, and_93_out);
  not not_22 (not_22_out, A[10]);
  xnor xnor_21 (xnor_21_out, A[11], B[20]);
  and and_83 (and_83_out, not_22_out, B[21]);
  not not_23 (not_23_out, A[9]);
  xnor xnor_22 (xnor_22_out, A[10], B[21]);
  xnor xnor_23 (xnor_23_out, A[9], B[22]);
  and and_84 (and_84_out, not_23_out, B[22]);
  not not_24 (not_24_out, A[8]);
  and and_85 (and_85_out, not_24_out, B[23]);
  not not_25 (not_25_out, A[7]);
  xnor xnor_24 (xnor_24_out, A[8], B[23]);
  and and_86 (and_86_out, not_25_out, B[24]);
  xnor xnor_25 (xnor_25_out, A[7], B[24]);
  not not_26 (not_26_out, A[6]);
  xnor xnor_26 (xnor_26_out, A[6], B[25]);
  and and_87 (and_87_out, not_26_out, B[25]);
  not not_27 (not_27_out, A[5]);
  and and_88 (and_88_out, not_27_out, B[26]);
  not not_28 (not_28_out, A[4]);
  xnor xnor_27 (xnor_27_out, A[5], B[26]);
  xnor xnor_28 (xnor_28_out, A[4], B[27]);
  and and_89 (and_89_out, not_28_out, B[27]);
  not not_29 (not_29_out, A[3]);
  and and_90 (and_90_out, not_29_out, B[28]);
  not not_30 (not_30_out, A[2]);
  xnor xnor_29 (xnor_29_out, A[3], B[28]);
  and and_91 (and_91_out, not_30_out, B[29]);
  not not_31 (not_31_out, A[1]);
  xnor xnor_30 (xnor_30_out, A[2], B[29]);
  xnor xnor_31 (xnor_31_out, A[1], B[30]);
  and and_92 (and_92_out, not_31_out, B[30]);
  not not_32 (not_32_out, A[0]);
  and and_93 (and_93_out, not_32_out, B[31]);

  assign out_3[31:1] = {31{1'b0}};

  // Notes on the sheet:
  //   1 if B > A
  //   1 if A < B, 0 Otherwise
  //   A > B = 0
  //   B > A = 1
  //   1 if A < B, 0 Otherwise
  //   1 if A < B, 0 Otherwise
endmodule

module Comparator (
  input  [31:0] A,
  input  [31:0] B,
  output [31:0] A___B
);

  Comparator_part #(.width(32)) comparator_1 (.a(A), .b(B), .gt(A___B[0]));  // open: eq, lt

  assign A___B[31:1] = {31{1'b0}};
endmodule

module main (
  input  [31:0] Input_A,
  input  [31:0] Input_B,
  input  Carry_In,
  input  [3:0] ALU_Control,
  input  [4:0] SHFT_AMMT,
  output [31:0] out_6,
  output Zero,
  output Carry_Out
);

  wire and_1_out, CLA_carry_out, n32b_subtract_1_carry_out, not_1_out, not_2_out, or_1_out;
  wire [0:0] and_2_out;
  wire [31:0] AND_32_a___b_32b, CLA_out_4, Comparator_a___b, LSHIFT_output, multiplexer_2_out,
       n32b_subtract_1_out_4, NOR_32_a___b_32b, OR_32_a___b_32b, RSHIFT_output, XOR_32_a___b_32b;

  or or_1 (or_1_out, and_1_out, ALU_Control[0]);
  and and_1 (and_1_out, not_2_out, ALU_Control[2], not_1_out);
  not not_1 (not_1_out, ALU_Control[1]);
  not not_2 (not_2_out, ALU_Control[3]);
  AND_32 AND_32 (._32B_A(Input_A), ._32b_B(Input_B), .A___B_32B(AND_32_a___b_32b));
  OR_32 OR_32 (._32B_A(Input_A), ._32b_B(Input_B), .A___B_32B(OR_32_a___b_32b));
  CLA__Carry_lookahead_adder CLA (
    .A(Input_A), .B(Input_B), .Carry_In(Carry_In), .Carry_Out(CLA_carry_out), .out_4(CLA_out_4));
  _32b_Subtract u_32b_subtract_1 (
    .A(Input_A), .B(Input_B), .Carry_In(Carry_In), .Carry_Out(n32b_subtract_1_carry_out),
    .out_4(n32b_subtract_1_out_4));
  Comparator Comparator (.A(Input_A), .B(Input_B), .A___B(Comparator_a___b));
  NOR_32 NOR_32 (._32B_A(Input_A), ._32b_B(Input_B), .A___B_32B(NOR_32_a___b_32b));
  XOR_32 XOR_32 (._32B_A(Input_A), ._32b_B(Input_B), .A___B_32B(XOR_32_a___b_32b));
  Shift_Right RSHIFT (
    .in_2(ALU_Control[0]), .in_3(SHFT_AMMT[4]), .in_4(SHFT_AMMT[3]), .in_5(SHFT_AMMT[2]),
    .in_6(SHFT_AMMT[1]), .in_7(SHFT_AMMT[0]), .Input(Input_A), .OUTPUT(RSHIFT_output));
  Multiplexer multiplexer_1 (
    .in0(n32b_subtract_1_carry_out), .in1(CLA_carry_out), .out(Carry_Out), .sel(or_1_out));  // open: en
  Shift_Left LSHIFT (
    .in_2(SHFT_AMMT[4]), .in_3(SHFT_AMMT[3]), .in_4(SHFT_AMMT[2]), .in_5(SHFT_AMMT[1]), .in_6(SHFT_AMMT[0]),
    .Input(Input_A), .OUTPUT(LSHIFT_output));
  Multiplexer #(.select(3), .width(32)) multiplexer_2 (
    .in0(AND_32_a___b_32b), .in1(OR_32_a___b_32b), .in2(NOR_32_a___b_32b), .in3(XOR_32_a___b_32b),
    .in4(CLA_out_4), .in5(n32b_subtract_1_out_4), .in6(Comparator_a___b), .in7(Input_A),
    .out(multiplexer_2_out), .sel(ALU_Control[2:0]));  // open: en
  Multiplexer #(.select(2), .width(32)) multiplexer_3 (
    .in0(multiplexer_2_out), .in2(LSHIFT_output), .in3(RSHIFT_output), .out(out_6),
    .sel({ALU_Control[3], and_2_out[0]}));  // open: in1, en
  and and_2 (and_2_out[0], ALU_Control[1], ALU_Control[3]);
  R_Zero u_Zero (.in_1(out_6), .out_2(Zero));

  // Notes on the sheet:
  //   ( Mips has no carry )
  //   32 Bit Carry Look Ahead (CLA) Adder
  //   1 if A < B, 0 Otherwise
  //   Transmitting Shift Ammount to Shifters if chosen
  //   Subbtractor
  //   Outputs simple bit if result is Zero
endmodule
